// Logisim project ula.circ as structural Verilog: 15 circuits, main circuit MicroPro
module main (
  input  RESET,
  output [31:0] out_2,
  output [31:0] out_3
);

  wire clock_1_out, not_1_out;
  wire [7:0] micropro_1_addr;
  wire [31:0] ram_1_data;

  RAM #(.dataWidth(32)) ram_1 (.addr(micropro_1_addr), .data(ram_1_data));  // open: sel, clk, ld, clr
  not not_1 (not_1_out, clock_1_out);
  Clock clock_1 (.out(clock_1_out));
  MicroPro micropro_1 (
    .in_1(ram_1_data), .CLK(clock_1_out), .RESET(RESET), .wr(not_1_out), .S(out_3), .Addr(micropro_1_addr));  // open: OverFlow, Zero, out_5, out_6
endmodule

module MicroPro (
  input  [31:0] in_1,
  input  CLK,
  input  RESET,
  input  wr,
  output [31:0] out_5,
  output [31:0] out_6,
  output [7:0] Addr,
  output [31:0] S,
  output OverFlow,
  output Zero
);

  wire and_1_out, and_2_out, and_3_out, not_1_out, or_1_out;
  wire [31:0] multiplexer_1_out;

  and and_1 (and_1_out, in_1[31], in_1[30], in_1[29], in_1[28], in_1[27]);
  pc pc_1 (.Clk(CLK), .RESET(RESET), .Jump(or_1_out), .Const(in_1[7:0]), .Addr(Addr));
  or or_1 (or_1_out, and_1_out, and_2_out, and_3_out);
  and and_2 (and_2_out, in_1[29], in_1[31], in_1[30], in_1[28], ~in_1[27], Zero);  // AND_Gate
  and and_3 (and_3_out, in_1[29], in_1[31], in_1[30], ~in_1[28], in_1[27], not_1_out);  // AND_Gate
  not not_1 (not_1_out, Zero);
  Multiplexer #(.select(5), .width(32), .enable("false")) multiplexer_1 (
    .in0(out_6), .in1(out_6), .in2(out_6), .in3(out_6), .in4(out_6), .in5(out_6), .in6(out_6), .in7(out_6),
    .in8(out_6), .in9(out_6), .in10(out_6), .in11(out_6), .in12({{21{in_1[11]}}, in_1[10:0]}), .in29(out_6),
    .in30(out_6), .out(multiplexer_1_out), .sel(in_1[31:27]));  // open: in13, in14, in15, in16, in17, in18, in19, in20, in21, in22, in23, in24, in25, in26, in27, in28, in31
  ula ula_1 (
    .A(out_5), .B(multiplexer_1_out), .S(S), .OverFlow(OverFlow), .OpeCode(in_1[31:27]), .move(in_1[4:0]),
    .zero(Zero));
  bancoDeRes bancoderes_1 (
    .seletorRegistrador(in_1[26:22]), .a(S), .seletor_registrador_B(in_1[16:12]),
    .seletor_registrador_A(in_1[21:17]), .A_2(out_5), .B(out_6), .wr(wr));

  // Notes on the sheet:
  //   00000 - And
  //   00001 - Or
  //   00010 - XOR
  //   00011 - NAND
  //   00100 - Soma naturais
  //   00101 - Soma inteiros
  //   00110 - Subtração
  //   00111 - Deslocamento Esquerda
  //   01000 - Deslocamento Direita
  //   01001 - Deslocamento Direita Aritimética
  //   01010 - ROL
  //   01011 - SLT
  //   01100 - Soma Constante
  //   11101 - BNE (Branch if Not Equals)
  //   11110 - BEQ (Branch if EQuals)
  //   11111 - JMP
endmodule

module ula_cel (
  input  a,
  input  b,
  input  Cin,
  input  [4:0] Select,
  output S,
  output Cout
);

  wire and_1_out, full_adder_1_s, nand_1_out, or_1_out, xor_1_out;

  and and_1 (and_1_out, a, b);
  or or_1 (or_1_out, a, b);
  xor xor_1 (xor_1_out, a, b);
  nand nand_1 (nand_1_out, a, b);
  full_adder full_adder_1 (.in_3(Select), .Cin(Cin), .a(a), .b(b), .s(full_adder_1_s), .Cout(Cout));
  Multiplexer #(.select(5), .enable("false")) multiplexer_1 (
    .in0(and_1_out), .in1(or_1_out), .in2(xor_1_out), .in3(nand_1_out), .in4(full_adder_1_s),
    .in5(full_adder_1_s), .in6(full_adder_1_s), .in7(b), .in8(b), .in9(b), .in10(b), .in11(full_adder_1_s),
    .in12(full_adder_1_s), .in29(full_adder_1_s), .in30(full_adder_1_s), .out(S), .sel(Select));  // open: in13, in14, in15, in16, in17, in18, in19, in20, in21, in22, in23, in24, in25, in26, in27, in28, in31

  // Notes on the sheet:
  //   00000 - And
  //   00001 - Or
  //   00010 - XOR
  //   00011 - NAND
  //   00100 - Soma naturais
  //   00101 - Soma inteiros
  //   00110 - Subtração
endmodule

module full_adder (
  input  a,
  input  b,
  input  [4:0] in_3,
  input  Cin,
  output Cout,
  output s
);

  wire and_1_out, and_2_out, and_3_out, and_4_out, and_5_out, and_6_out, and_7_out, and_8_out,
       multiplexer_1_out, not_1_out, or_1_out, xor_1_out;

  and and_1 (and_1_out, ~in_3[0], in_3[1], in_3[2], ~in_3[3], ~in_3[4]);  // AND_Gate
  and and_2 (and_2_out, in_3[0], in_3[1], ~in_3[2], in_3[3], ~in_3[4]);  // AND_Gate
  and and_3 (and_3_out, ~in_3[0], in_3[1], in_3[2], in_3[3], in_3[4]);  // AND_Gate
  and and_4 (and_4_out, in_3[0], ~in_3[1], in_3[2], in_3[3], in_3[4]);  // AND_Gate
  or or_1 (or_1_out, and_1_out, and_2_out, and_3_out, and_4_out);
  not not_1 (not_1_out, b);
  Multiplexer #(.enable("false")) multiplexer_1 (.in0(b), .in1(not_1_out), .out(multiplexer_1_out), .sel(or_1_out));
  xor xor_1 (xor_1_out, a, multiplexer_1_out);
  xor xor_2 (s, xor_1_out, Cin);
  and and_5 (and_5_out, ~a, multiplexer_1_out, Cin);  // AND_Gate
  and and_6 (and_6_out, a, ~multiplexer_1_out, Cin);  // AND_Gate
  and and_7 (and_7_out, a, multiplexer_1_out, ~Cin);  // AND_Gate
  and and_8 (and_8_out, a, multiplexer_1_out, Cin);
  or or_2 (Cout, and_5_out, and_6_out, and_7_out, and_8_out);
endmodule

module overflow (
  input  Cin,
  input  S,
  input  b,
  input  a,
  input  [4:0] OpeCode,
  output OverFlow
);

  wire and_1_out, and_2_out, and_3_out, and_4_out, and_5_out, and_6_out, or_1_out, or_2_out;

  and and_1 (and_1_out, ~OpeCode[0], OpeCode[1], OpeCode[2], ~OpeCode[3], ~OpeCode[4]);  // AND_Gate
  and and_2 (and_2_out, OpeCode[0], OpeCode[1], ~OpeCode[2], OpeCode[3], ~OpeCode[4]);  // AND_Gate
  and and_3 (and_3_out, ~OpeCode[0], OpeCode[1], OpeCode[2], OpeCode[3], OpeCode[4]);  // AND_Gate
  and and_4 (and_4_out, OpeCode[0], ~OpeCode[1], OpeCode[2], OpeCode[3], OpeCode[4]);  // AND_Gate
  and and_5 (and_5_out, ~S, b, a);  // AND_Gate
  and and_6 (and_6_out, S, ~b, ~a);  // AND_Gate
  or or_1 (or_1_out, and_1_out, and_2_out, and_3_out, and_4_out);
  or or_2 (or_2_out, and_5_out, and_6_out);
  Multiplexer #(.enable("false")) multiplexer_1 (.in0(Cin), .in1(or_2_out), .out(OverFlow), .sel(or_1_out));

  // Notes on the sheet:
  //   00100 - Soma naturais
  //   00101 - Soma inteiros
endmodule

module deslocador (
  input  [31:0] A,
  input  [4:0] move,
  input  [4:0] OpeCode,
  output [31:0] S
);

  wire and_2_out, and_3_out, not_1_out, not_2_out, not_3_out, not_4_out, not_5_out, not_6_out, not_7_out,
       not_8_out;
  wire [1:0] or_1_out;
  wire [4:0] undriven;
  wire [31:0] desldir_1_s, desldirart_1_s, deslesq_1_s, rol_1_s;

  deslEsq deslesq_1 (.A(A), .Move(move), .S(deslesq_1_s));
  deslDir desldir_1 (.A(A), .Move(move), .S(desldir_1_s));
  deslDirArt desldirart_1 (.A(A), .Move(move), .S(desldirart_1_s));
  rol rol_1 (.A(A), .Move(move), .S(rol_1_s));
  not not_1 (not_1_out, undriven[4]);
  not not_2 (not_2_out, undriven[2]);
  not not_3 (not_3_out, undriven[1]);
  not not_4 (not_4_out, undriven[4]);
  not not_5 (not_5_out, undriven[3]);
  not not_6 (not_6_out, undriven[4]);
  not not_7 (not_7_out, undriven[2]);
  not not_8 (not_8_out, undriven[1]);
  and and_1 (or_1_out[1], not_1_out, undriven[3], not_2_out, not_3_out);
  and and_2 (and_2_out, not_4_out, not_5_out, undriven[2], undriven[1], undriven[0]);
  and and_3 (and_3_out, not_6_out, undriven[3], not_7_out, not_8_out, undriven[0]);
  Multiplexer #(.select(5), .width(32), .enable("false")) multiplexer_1 (
    .in0(A), .in1(A), .in2(A), .in3(A), .in4(A), .in5(A), .in6(A), .in7(deslesq_1_s), .in8(desldir_1_s),
    .in9(desldirart_1_s), .in10(rol_1_s), .in11(A), .in12(A), .in13(A), .in14(A), .in15(A), .in16(A),
    .in17(A), .in18(A), .in19(A), .in20(A), .in21(A), .in22(A), .in23(A), .in24(A), .in25(A), .in26(A),
    .in27(A), .in28(A), .in29(A), .in30(A), .in31(A), .out(S), .sel(OpeCode));
  or or_1 (or_1_out[0], and_2_out, and_3_out);

  // Notes on the sheet:
  //   00111 - 01
  //   01000 - 10
  //   01001 - 11
  //   xxxx - 00
endmodule

module deslEsq (
  input  [31:0] A,
  input  [4:0] Move,
  output [31:0] S
);

  wire multiplexer_1_out, multiplexer_2_out, multiplexer_3_out, multiplexer_4_out, multiplexer_5_out,
       multiplexer_6_out, multiplexer_7_out, multiplexer_8_out, multiplexer_9_out, multiplexer_10_out,
       multiplexer_11_out, multiplexer_12_out, multiplexer_13_out, multiplexer_14_out, multiplexer_15_out,
       multiplexer_16_out, multiplexer_17_out, multiplexer_18_out, multiplexer_19_out, multiplexer_20_out,
       multiplexer_21_out, multiplexer_22_out, multiplexer_23_out, multiplexer_24_out, multiplexer_25_out,
       multiplexer_26_out, multiplexer_27_out, multiplexer_28_out, multiplexer_29_out, multiplexer_30_out,
       multiplexer_31_out, multiplexer_32_out, multiplexer_33_out, multiplexer_34_out, multiplexer_35_out,
       multiplexer_36_out, multiplexer_37_out, multiplexer_38_out, multiplexer_39_out, multiplexer_40_out,
       multiplexer_41_out, multiplexer_42_out, multiplexer_43_out, multiplexer_44_out, multiplexer_45_out,
       multiplexer_46_out, multiplexer_47_out, multiplexer_48_out, multiplexer_49_out, multiplexer_50_out,
       multiplexer_51_out, multiplexer_52_out, multiplexer_53_out, multiplexer_54_out, multiplexer_55_out,
       multiplexer_56_out, multiplexer_57_out, multiplexer_58_out, multiplexer_59_out, multiplexer_60_out,
       multiplexer_61_out, multiplexer_62_out, multiplexer_63_out, multiplexer_64_out, multiplexer_65_out,
       multiplexer_66_out, multiplexer_67_out, multiplexer_68_out, multiplexer_69_out, multiplexer_70_out,
       multiplexer_71_out, multiplexer_72_out, multiplexer_73_out, multiplexer_74_out, multiplexer_75_out,
       multiplexer_76_out, multiplexer_77_out, multiplexer_78_out, multiplexer_79_out, multiplexer_80_out,
       multiplexer_81_out, multiplexer_82_out, multiplexer_83_out, multiplexer_84_out, multiplexer_85_out,
       multiplexer_86_out, multiplexer_87_out, multiplexer_88_out, multiplexer_89_out, multiplexer_90_out,
       multiplexer_91_out, multiplexer_92_out, multiplexer_93_out, multiplexer_94_out, multiplexer_95_out,
       multiplexer_96_out, multiplexer_97_out, multiplexer_98_out, multiplexer_99_out, multiplexer_100_out,
       multiplexer_101_out, multiplexer_102_out, multiplexer_103_out, multiplexer_104_out,
       multiplexer_105_out, multiplexer_106_out, multiplexer_107_out, multiplexer_108_out,
       multiplexer_109_out, multiplexer_110_out, multiplexer_111_out, multiplexer_112_out,
       multiplexer_113_out, multiplexer_114_out, multiplexer_115_out, multiplexer_116_out,
       multiplexer_117_out, multiplexer_118_out, multiplexer_119_out, multiplexer_120_out,
       multiplexer_121_out, multiplexer_122_out, multiplexer_123_out, multiplexer_124_out,
       multiplexer_125_out, multiplexer_126_out, multiplexer_127_out, multiplexer_128_out;

  Multiplexer #(.enable("false")) multiplexer_1 (.in0(A[31]), .in1(A[30]), .out(multiplexer_1_out), .sel(Move[0]));
  Multiplexer #(.enable("false")) multiplexer_2 (.in0(A[30]), .in1(A[29]), .out(multiplexer_2_out), .sel(Move[0]));
  Multiplexer #(.enable("false")) multiplexer_3 (.in0(A[29]), .in1(A[28]), .out(multiplexer_3_out), .sel(Move[0]));
  Multiplexer #(.enable("false")) multiplexer_4 (.in0(A[28]), .in1(A[27]), .out(multiplexer_4_out), .sel(Move[0]));
  Multiplexer #(.enable("false")) multiplexer_5 (.in0(A[27]), .in1(A[26]), .out(multiplexer_5_out), .sel(Move[0]));
  Multiplexer #(.enable("false")) multiplexer_6 (.in0(A[26]), .in1(A[25]), .out(multiplexer_6_out), .sel(Move[0]));
  Multiplexer #(.enable("false")) multiplexer_7 (.in0(A[25]), .in1(A[24]), .out(multiplexer_7_out), .sel(Move[0]));
  Multiplexer #(.enable("false")) multiplexer_8 (.in0(A[24]), .in1(A[23]), .out(multiplexer_8_out), .sel(Move[0]));
  Multiplexer #(.enable("false")) multiplexer_9 (.in0(A[23]), .in1(A[22]), .out(multiplexer_9_out), .sel(Move[0]));
  Multiplexer #(.enable("false")) multiplexer_10 (.in0(A[22]), .in1(A[21]), .out(multiplexer_10_out), .sel(Move[0]));
  Multiplexer #(.enable("false")) multiplexer_11 (.in0(A[21]), .in1(A[20]), .out(multiplexer_11_out), .sel(Move[0]));
  Multiplexer #(.enable("false")) multiplexer_12 (.in0(A[20]), .in1(A[19]), .out(multiplexer_12_out), .sel(Move[0]));
  Multiplexer #(.enable("false")) multiplexer_13 (.in0(A[19]), .in1(A[18]), .out(multiplexer_13_out), .sel(Move[0]));
  Multiplexer #(.enable("false")) multiplexer_14 (.in0(A[18]), .in1(A[17]), .out(multiplexer_14_out), .sel(Move[0]));
  Multiplexer #(.enable("false")) multiplexer_15 (.in0(A[17]), .in1(A[16]), .out(multiplexer_15_out), .sel(Move[0]));
  Multiplexer #(.enable("false")) multiplexer_16 (.in0(A[16]), .in1(A[15]), .out(multiplexer_16_out), .sel(Move[0]));
  Multiplexer #(.enable("false")) multiplexer_17 (.in0(A[15]), .in1(A[14]), .out(multiplexer_17_out), .sel(Move[0]));
  Multiplexer #(.enable("false")) multiplexer_18 (.in0(A[14]), .in1(A[13]), .out(multiplexer_18_out), .sel(Move[0]));
  Multiplexer #(.enable("false")) multiplexer_19 (.in0(A[13]), .in1(A[12]), .out(multiplexer_19_out), .sel(Move[0]));
  Multiplexer #(.enable("false")) multiplexer_20 (.in0(A[12]), .in1(A[11]), .out(multiplexer_20_out), .sel(Move[0]));
  Multiplexer #(.enable("false")) multiplexer_21 (.in0(A[11]), .in1(A[10]), .out(multiplexer_21_out), .sel(Move[0]));
  Multiplexer #(.enable("false")) multiplexer_22 (.in0(A[10]), .in1(A[9]), .out(multiplexer_22_out), .sel(Move[0]));
  Multiplexer #(.enable("false")) multiplexer_23 (.in0(A[9]), .in1(A[8]), .out(multiplexer_23_out), .sel(Move[0]));
  Multiplexer #(.enable("false")) multiplexer_24 (.in0(A[8]), .in1(A[7]), .out(multiplexer_24_out), .sel(Move[0]));
  Multiplexer #(.enable("false")) multiplexer_25 (.in0(A[7]), .in1(A[6]), .out(multiplexer_25_out), .sel(Move[0]));
  Multiplexer #(.enable("false")) multiplexer_26 (.in0(A[6]), .in1(A[5]), .out(multiplexer_26_out), .sel(Move[0]));
  Multiplexer #(.enable("false")) multiplexer_27 (.in0(A[5]), .in1(A[4]), .out(multiplexer_27_out), .sel(Move[0]));
  Multiplexer #(.enable("false")) multiplexer_28 (.in0(A[4]), .in1(A[3]), .out(multiplexer_28_out), .sel(Move[0]));
  Multiplexer #(.enable("false")) multiplexer_29 (.in0(A[3]), .in1(A[2]), .out(multiplexer_29_out), .sel(Move[0]));
  Multiplexer #(.enable("false")) multiplexer_30 (.in0(A[2]), .in1(A[1]), .out(multiplexer_30_out), .sel(Move[0]));
  Multiplexer #(.enable("false")) multiplexer_31 (.in0(A[1]), .in1(A[0]), .out(multiplexer_31_out), .sel(Move[0]));
  Multiplexer #(.enable("false")) multiplexer_32 (.in0(A[0]), .in1(1'b0), .out(multiplexer_32_out), .sel(Move[0]));
  Multiplexer #(.enable("false")) multiplexer_33 (
    .in0(multiplexer_1_out), .in1(multiplexer_3_out), .out(multiplexer_33_out), .sel(Move[1]));
  Multiplexer #(.enable("false")) multiplexer_34 (
    .in0(multiplexer_2_out), .in1(multiplexer_4_out), .out(multiplexer_34_out), .sel(Move[1]));
  Multiplexer #(.enable("false")) multiplexer_35 (
    .in0(multiplexer_3_out), .in1(multiplexer_5_out), .out(multiplexer_35_out), .sel(Move[1]));
  Multiplexer #(.enable("false")) multiplexer_36 (
    .in0(multiplexer_4_out), .in1(multiplexer_6_out), .out(multiplexer_36_out), .sel(Move[1]));
  Multiplexer #(.enable("false")) multiplexer_37 (
    .in0(multiplexer_5_out), .in1(multiplexer_7_out), .out(multiplexer_37_out), .sel(Move[1]));
  Multiplexer #(.enable("false")) multiplexer_38 (
    .in0(multiplexer_6_out), .in1(multiplexer_8_out), .out(multiplexer_38_out), .sel(Move[1]));
  Multiplexer #(.enable("false")) multiplexer_39 (
    .in0(multiplexer_7_out), .in1(multiplexer_9_out), .out(multiplexer_39_out), .sel(Move[1]));
  Multiplexer #(.enable("false")) multiplexer_40 (
    .in0(multiplexer_8_out), .in1(multiplexer_10_out), .out(multiplexer_40_out), .sel(Move[1]));
  Multiplexer #(.enable("false")) multiplexer_41 (
    .in0(multiplexer_9_out), .in1(multiplexer_11_out), .out(multiplexer_41_out), .sel(Move[1]));
  Multiplexer #(.enable("false")) multiplexer_42 (
    .in0(multiplexer_10_out), .in1(multiplexer_12_out), .out(multiplexer_42_out), .sel(Move[1]));
  Multiplexer #(.enable("false")) multiplexer_43 (
    .in0(multiplexer_11_out), .in1(multiplexer_13_out), .out(multiplexer_43_out), .sel(Move[1]));
  Multiplexer #(.enable("false")) multiplexer_44 (
    .in0(multiplexer_12_out), .in1(multiplexer_14_out), .out(multiplexer_44_out), .sel(Move[1]));
  Multiplexer #(.enable("false")) multiplexer_45 (
    .in0(multiplexer_13_out), .in1(multiplexer_15_out), .out(multiplexer_45_out), .sel(Move[1]));
  Multiplexer #(.enable("false")) multiplexer_46 (
    .in0(multiplexer_14_out), .in1(multiplexer_16_out), .out(multiplexer_46_out), .sel(Move[1]));
  Multiplexer #(.enable("false")) multiplexer_47 (
    .in0(multiplexer_15_out), .in1(multiplexer_17_out), .out(multiplexer_47_out), .sel(Move[1]));
  Multiplexer #(.enable("false")) multiplexer_48 (
    .in0(multiplexer_16_out), .in1(multiplexer_18_out), .out(multiplexer_48_out), .sel(Move[1]));
  Multiplexer #(.enable("false")) multiplexer_49 (
    .in0(multiplexer_17_out), .in1(multiplexer_19_out), .out(multiplexer_49_out), .sel(Move[1]));
  Multiplexer #(.enable("false")) multiplexer_50 (
    .in0(multiplexer_18_out), .in1(multiplexer_20_out), .out(multiplexer_50_out), .sel(Move[1]));
  Multiplexer #(.enable("false")) multiplexer_51 (
    .in0(multiplexer_19_out), .in1(multiplexer_21_out), .out(multiplexer_51_out), .sel(Move[1]));
  Multiplexer #(.enable("false")) multiplexer_52 (
    .in0(multiplexer_20_out), .in1(multiplexer_22_out), .out(multiplexer_52_out), .sel(Move[1]));
  Multiplexer #(.enable("false")) multiplexer_53 (
    .in0(multiplexer_21_out), .in1(multiplexer_23_out), .out(multiplexer_53_out), .sel(Move[1]));
  Multiplexer #(.enable("false")) multiplexer_54 (
    .in0(multiplexer_22_out), .in1(multiplexer_24_out), .out(multiplexer_54_out), .sel(Move[1]));
  Multiplexer #(.enable("false")) multiplexer_55 (
    .in0(multiplexer_23_out), .in1(multiplexer_25_out), .out(multiplexer_55_out), .sel(Move[1]));
  Multiplexer #(.enable("false")) multiplexer_56 (
    .in0(multiplexer_24_out), .in1(multiplexer_26_out), .out(multiplexer_56_out), .sel(Move[1]));
  Multiplexer #(.enable("false")) multiplexer_57 (
    .in0(multiplexer_25_out), .in1(multiplexer_27_out), .out(multiplexer_57_out), .sel(Move[1]));
  Multiplexer #(.enable("false")) multiplexer_58 (
    .in0(multiplexer_26_out), .in1(multiplexer_28_out), .out(multiplexer_58_out), .sel(Move[1]));
  Multiplexer #(.enable("false")) multiplexer_59 (
    .in0(multiplexer_27_out), .in1(multiplexer_29_out), .out(multiplexer_59_out), .sel(Move[1]));
  Multiplexer #(.enable("false")) multiplexer_60 (
    .in0(multiplexer_28_out), .in1(multiplexer_30_out), .out(multiplexer_60_out), .sel(Move[1]));
  Multiplexer #(.enable("false")) multiplexer_61 (
    .in0(multiplexer_29_out), .in1(multiplexer_31_out), .out(multiplexer_61_out), .sel(Move[1]));
  Multiplexer #(.enable("false")) multiplexer_62 (
    .in0(multiplexer_30_out), .in1(multiplexer_32_out), .out(multiplexer_62_out), .sel(Move[1]));
  Multiplexer #(.enable("false")) multiplexer_63 (
    .in0(multiplexer_31_out), .in1(1'b0), .out(multiplexer_63_out), .sel(Move[1]));
  Multiplexer #(.enable("false")) multiplexer_64 (
    .in0(multiplexer_32_out), .in1(1'b0), .out(multiplexer_64_out), .sel(Move[1]));
  Multiplexer #(.enable("false")) multiplexer_65 (
    .in0(multiplexer_33_out), .in1(multiplexer_37_out), .out(multiplexer_65_out), .sel(Move[2]));
  Multiplexer #(.enable("false")) multiplexer_66 (
    .in0(multiplexer_34_out), .in1(multiplexer_38_out), .out(multiplexer_66_out), .sel(Move[2]));
  Multiplexer #(.enable("false")) multiplexer_67 (
    .in0(multiplexer_35_out), .in1(multiplexer_39_out), .out(multiplexer_67_out), .sel(Move[2]));
  Multiplexer #(.enable("false")) multiplexer_68 (
    .in0(multiplexer_36_out), .in1(multiplexer_40_out), .out(multiplexer_68_out), .sel(Move[2]));
  Multiplexer #(.enable("false")) multiplexer_69 (
    .in0(multiplexer_37_out), .in1(multiplexer_41_out), .out(multiplexer_69_out), .sel(Move[2]));
  Multiplexer #(.enable("false")) multiplexer_70 (
    .in0(multiplexer_38_out), .in1(multiplexer_42_out), .out(multiplexer_70_out), .sel(Move[2]));
  Multiplexer #(.enable("false")) multiplexer_71 (
    .in0(multiplexer_39_out), .in1(multiplexer_43_out), .out(multiplexer_71_out), .sel(Move[2]));
  Multiplexer #(.enable("false")) multiplexer_72 (
    .in0(multiplexer_40_out), .in1(multiplexer_44_out), .out(multiplexer_72_out), .sel(Move[2]));
  Multiplexer #(.enable("false")) multiplexer_73 (
    .in0(multiplexer_41_out), .in1(multiplexer_45_out), .out(multiplexer_73_out), .sel(Move[2]));
  Multiplexer #(.enable("false")) multiplexer_74 (
    .in0(multiplexer_42_out), .in1(multiplexer_46_out), .out(multiplexer_74_out), .sel(Move[2]));
  Multiplexer #(.enable("false")) multiplexer_75 (
    .in0(multiplexer_43_out), .in1(multiplexer_47_out), .out(multiplexer_75_out), .sel(Move[2]));
  Multiplexer #(.enable("false")) multiplexer_76 (
    .in0(multiplexer_44_out), .in1(multiplexer_48_out), .out(multiplexer_76_out), .sel(Move[2]));
  Multiplexer #(.enable("false")) multiplexer_77 (
    .in0(multiplexer_45_out), .in1(multiplexer_49_out), .out(multiplexer_77_out), .sel(Move[2]));
  Multiplexer #(.enable("false")) multiplexer_78 (
    .in0(multiplexer_46_out), .in1(multiplexer_50_out), .out(multiplexer_78_out), .sel(Move[2]));
  Multiplexer #(.enable("false")) multiplexer_79 (
    .in0(multiplexer_47_out), .in1(multiplexer_51_out), .out(multiplexer_79_out), .sel(Move[2]));
  Multiplexer #(.enable("false")) multiplexer_80 (
    .in0(multiplexer_48_out), .in1(multiplexer_52_out), .out(multiplexer_80_out), .sel(Move[2]));
  Multiplexer #(.enable("false")) multiplexer_81 (
    .in0(multiplexer_49_out), .in1(multiplexer_53_out), .out(multiplexer_81_out), .sel(Move[2]));
  Multiplexer #(.enable("false")) multiplexer_82 (
    .in0(multiplexer_50_out), .in1(multiplexer_54_out), .out(multiplexer_82_out), .sel(Move[2]));
  Multiplexer #(.enable("false")) multiplexer_83 (
    .in0(multiplexer_51_out), .in1(multiplexer_55_out), .out(multiplexer_83_out), .sel(Move[2]));
  Multiplexer #(.enable("false")) multiplexer_84 (
    .in0(multiplexer_52_out), .in1(multiplexer_56_out), .out(multiplexer_84_out), .sel(Move[2]));
  Multiplexer #(.enable("false")) multiplexer_85 (
    .in0(multiplexer_53_out), .in1(multiplexer_57_out), .out(multiplexer_85_out), .sel(Move[2]));
  Multiplexer #(.enable("false")) multiplexer_86 (
    .in0(multiplexer_54_out), .in1(multiplexer_58_out), .out(multiplexer_86_out), .sel(Move[2]));
  Multiplexer #(.enable("false")) multiplexer_87 (
    .in0(multiplexer_55_out), .in1(multiplexer_59_out), .out(multiplexer_87_out), .sel(Move[2]));
  Multiplexer #(.enable("false")) multiplexer_88 (
    .in0(multiplexer_56_out), .in1(multiplexer_60_out), .out(multiplexer_88_out), .sel(Move[2]));
  Multiplexer #(.enable("false")) multiplexer_89 (
    .in0(multiplexer_57_out), .in1(multiplexer_61_out), .out(multiplexer_89_out), .sel(Move[2]));
  Multiplexer #(.enable("false")) multiplexer_90 (
    .in0(multiplexer_58_out), .in1(multiplexer_62_out), .out(multiplexer_90_out), .sel(Move[2]));
  Multiplexer #(.enable("false")) multiplexer_91 (
    .in0(multiplexer_59_out), .in1(multiplexer_63_out), .out(multiplexer_91_out), .sel(Move[2]));
  Multiplexer #(.enable("false")) multiplexer_92 (
    .in0(multiplexer_60_out), .in1(multiplexer_64_out), .out(multiplexer_92_out), .sel(Move[2]));
  Multiplexer #(.enable("false")) multiplexer_93 (
    .in0(multiplexer_61_out), .in1(1'b0), .out(multiplexer_93_out), .sel(Move[2]));
  Multiplexer #(.enable("false")) multiplexer_94 (
    .in0(multiplexer_62_out), .in1(1'b0), .out(multiplexer_94_out), .sel(Move[2]));
  Multiplexer #(.enable("false")) multiplexer_95 (
    .in0(multiplexer_63_out), .in1(1'b0), .out(multiplexer_95_out), .sel(Move[2]));
  Multiplexer #(.enable("false")) multiplexer_96 (
    .in0(multiplexer_64_out), .in1(1'b0), .out(multiplexer_96_out), .sel(Move[2]));
  Multiplexer #(.enable("false")) multiplexer_97 (
    .in0(multiplexer_65_out), .in1(multiplexer_73_out), .out(multiplexer_97_out), .sel(Move[3]));
  Multiplexer #(.enable("false")) multiplexer_98 (
    .in0(multiplexer_66_out), .in1(multiplexer_74_out), .out(multiplexer_98_out), .sel(Move[3]));
  Multiplexer #(.enable("false")) multiplexer_99 (
    .in0(multiplexer_67_out), .in1(multiplexer_75_out), .out(multiplexer_99_out), .sel(Move[3]));
  Multiplexer #(.enable("false")) multiplexer_100 (
    .in0(multiplexer_68_out), .in1(multiplexer_76_out), .out(multiplexer_100_out), .sel(Move[3]));
  Multiplexer #(.enable("false")) multiplexer_101 (
    .in0(multiplexer_69_out), .in1(multiplexer_77_out), .out(multiplexer_101_out), .sel(Move[3]));
  Multiplexer #(.enable("false")) multiplexer_102 (
    .in0(multiplexer_70_out), .in1(multiplexer_78_out), .out(multiplexer_102_out), .sel(Move[3]));
  Multiplexer #(.enable("false")) multiplexer_103 (
    .in0(multiplexer_71_out), .in1(multiplexer_79_out), .out(multiplexer_103_out), .sel(Move[3]));
  Multiplexer #(.enable("false")) multiplexer_104 (
    .in0(multiplexer_72_out), .in1(multiplexer_80_out), .out(multiplexer_104_out), .sel(Move[3]));
  Multiplexer #(.enable("false")) multiplexer_105 (
    .in0(multiplexer_73_out), .in1(multiplexer_81_out), .out(multiplexer_105_out), .sel(Move[3]));
  Multiplexer #(.enable("false")) multiplexer_106 (
    .in0(multiplexer_74_out), .in1(multiplexer_82_out), .out(multiplexer_106_out), .sel(Move[3]));
  Multiplexer #(.enable("false")) multiplexer_107 (
    .in0(multiplexer_75_out), .in1(multiplexer_83_out), .out(multiplexer_107_out), .sel(Move[3]));
  Multiplexer #(.enable("false")) multiplexer_108 (
    .in0(multiplexer_76_out), .in1(multiplexer_84_out), .out(multiplexer_108_out), .sel(Move[3]));
  Multiplexer #(.enable("false")) multiplexer_109 (
    .in0(multiplexer_77_out), .in1(multiplexer_85_out), .out(multiplexer_109_out), .sel(Move[3]));
  Multiplexer #(.enable("false")) multiplexer_110 (
    .in0(multiplexer_78_out), .in1(multiplexer_86_out), .out(multiplexer_110_out), .sel(Move[3]));
  Multiplexer #(.enable("false")) multiplexer_111 (
    .in0(multiplexer_79_out), .in1(multiplexer_87_out), .out(multiplexer_111_out), .sel(Move[3]));
  Multiplexer #(.enable("false")) multiplexer_112 (
    .in0(multiplexer_80_out), .in1(multiplexer_88_out), .out(multiplexer_112_out), .sel(Move[3]));
  Multiplexer #(.enable("false")) multiplexer_113 (
    .in0(multiplexer_81_out), .in1(multiplexer_89_out), .out(multiplexer_113_out), .sel(Move[3]));
  Multiplexer #(.enable("false")) multiplexer_114 (
    .in0(multiplexer_82_out), .in1(multiplexer_90_out), .out(multiplexer_114_out), .sel(Move[3]));
  Multiplexer #(.enable("false")) multiplexer_115 (
    .in0(multiplexer_83_out), .in1(multiplexer_91_out), .out(multiplexer_115_out), .sel(Move[3]));
  Multiplexer #(.enable("false")) multiplexer_116 (
    .in0(multiplexer_84_out), .in1(multiplexer_92_out), .out(multiplexer_116_out), .sel(Move[3]));
  Multiplexer #(.enable("false")) multiplexer_117 (
    .in0(multiplexer_85_out), .in1(multiplexer_93_out), .out(multiplexer_117_out), .sel(Move[3]));
  Multiplexer #(.enable("false")) multiplexer_118 (
    .in0(multiplexer_86_out), .in1(multiplexer_94_out), .out(multiplexer_118_out), .sel(Move[3]));
  Multiplexer #(.enable("false")) multiplexer_119 (
    .in0(multiplexer_87_out), .in1(multiplexer_95_out), .out(multiplexer_119_out), .sel(Move[3]));
  Multiplexer #(.enable("false")) multiplexer_120 (
    .in0(multiplexer_88_out), .in1(multiplexer_96_out), .out(multiplexer_120_out), .sel(Move[3]));
  Multiplexer #(.enable("false")) multiplexer_121 (
    .in0(multiplexer_89_out), .in1(1'b0), .out(multiplexer_121_out), .sel(Move[3]));
  Multiplexer #(.enable("false")) multiplexer_122 (
    .in0(multiplexer_90_out), .in1(1'b0), .out(multiplexer_122_out), .sel(Move[3]));
  Multiplexer #(.enable("false")) multiplexer_123 (
    .in0(multiplexer_91_out), .in1(1'b0), .out(multiplexer_123_out), .sel(Move[3]));
  Multiplexer #(.enable("false")) multiplexer_124 (
    .in0(multiplexer_92_out), .in1(1'b0), .out(multiplexer_124_out), .sel(Move[3]));
  Multiplexer #(.enable("false")) multiplexer_125 (
    .in0(multiplexer_93_out), .in1(1'b0), .out(multiplexer_125_out), .sel(Move[3]));
  Multiplexer #(.enable("false")) multiplexer_126 (
    .in0(multiplexer_94_out), .in1(1'b0), .out(multiplexer_126_out), .sel(Move[3]));
  Multiplexer #(.enable("false")) multiplexer_127 (
    .in0(multiplexer_95_out), .in1(1'b0), .out(multiplexer_127_out), .sel(Move[3]));
  Multiplexer #(.enable("false")) multiplexer_128 (
    .in0(multiplexer_96_out), .in1(1'b0), .out(multiplexer_128_out), .sel(Move[3]));
  Multiplexer #(.enable("false")) multiplexer_129 (
    .in0(multiplexer_97_out), .in1(multiplexer_113_out), .out(S[31]), .sel(Move[4]));
  Multiplexer #(.enable("false")) multiplexer_130 (
    .in0(multiplexer_98_out), .in1(multiplexer_114_out), .out(S[30]), .sel(Move[4]));
  Multiplexer #(.enable("false")) multiplexer_131 (
    .in0(multiplexer_99_out), .in1(multiplexer_115_out), .out(S[29]), .sel(Move[4]));
  Multiplexer #(.enable("false")) multiplexer_132 (
    .in0(multiplexer_100_out), .in1(multiplexer_116_out), .out(S[28]), .sel(Move[4]));
  Multiplexer #(.enable("false")) multiplexer_133 (
    .in0(multiplexer_101_out), .in1(multiplexer_117_out), .out(S[27]), .sel(Move[4]));
  Multiplexer #(.enable("false")) multiplexer_134 (
    .in0(multiplexer_102_out), .in1(multiplexer_118_out), .out(S[26]), .sel(Move[4]));
  Multiplexer #(.enable("false")) multiplexer_135 (
    .in0(multiplexer_103_out), .in1(multiplexer_119_out), .out(S[25]), .sel(Move[4]));
  Multiplexer #(.enable("false")) multiplexer_136 (
    .in0(multiplexer_104_out), .in1(multiplexer_120_out), .out(S[24]), .sel(Move[4]));
  Multiplexer #(.enable("false")) multiplexer_137 (
    .in0(multiplexer_105_out), .in1(multiplexer_121_out), .out(S[23]), .sel(Move[4]));
  Multiplexer #(.enable("false")) multiplexer_138 (
    .in0(multiplexer_106_out), .in1(multiplexer_122_out), .out(S[22]), .sel(Move[4]));
  Multiplexer #(.enable("false")) multiplexer_139 (
    .in0(multiplexer_107_out), .in1(multiplexer_123_out), .out(S[21]), .sel(Move[4]));
  Multiplexer #(.enable("false")) multiplexer_140 (
    .in0(multiplexer_108_out), .in1(multiplexer_124_out), .out(S[20]), .sel(Move[4]));
  Multiplexer #(.enable("false")) multiplexer_141 (
    .in0(multiplexer_109_out), .in1(multiplexer_125_out), .out(S[19]), .sel(Move[4]));
  Multiplexer #(.enable("false")) multiplexer_142 (
    .in0(multiplexer_110_out), .in1(multiplexer_126_out), .out(S[18]), .sel(Move[4]));
  Multiplexer #(.enable("false")) multiplexer_143 (
    .in0(multiplexer_111_out), .in1(multiplexer_127_out), .out(S[17]), .sel(Move[4]));
  Multiplexer #(.enable("false")) multiplexer_144 (
    .in0(multiplexer_112_out), .in1(multiplexer_128_out), .out(S[16]), .sel(Move[4]));
  Multiplexer #(.enable("false")) multiplexer_145 (.in0(multiplexer_113_out), .in1(1'b0), .out(S[15]), .sel(Move[4]));
  Multiplexer #(.enable("false")) multiplexer_146 (.in0(multiplexer_114_out), .in1(1'b0), .out(S[14]), .sel(Move[4]));
  Multiplexer #(.enable("false")) multiplexer_147 (.in0(multiplexer_115_out), .in1(1'b0), .out(S[13]), .sel(Move[4]));
  Multiplexer #(.enable("false")) multiplexer_148 (.in0(multiplexer_116_out), .in1(1'b0), .out(S[12]), .sel(Move[4]));
  Multiplexer #(.enable("false")) multiplexer_149 (.in0(multiplexer_117_out), .in1(1'b0), .out(S[11]), .sel(Move[4]));
  Multiplexer #(.enable("false")) multiplexer_150 (.in0(multiplexer_118_out), .in1(1'b0), .out(S[10]), .sel(Move[4]));
  Multiplexer #(.enable("false")) multiplexer_151 (.in0(multiplexer_119_out), .in1(1'b0), .out(S[9]), .sel(Move[4]));
  Multiplexer #(.enable("false")) multiplexer_152 (.in0(multiplexer_120_out), .in1(1'b0), .out(S[8]), .sel(Move[4]));
  Multiplexer #(.enable("false")) multiplexer_153 (.in0(multiplexer_121_out), .in1(1'b0), .out(S[7]), .sel(Move[4]));
  Multiplexer #(.enable("false")) multiplexer_154 (.in0(multiplexer_122_out), .in1(1'b0), .out(S[6]), .sel(Move[4]));
  Multiplexer #(.enable("false")) multiplexer_155 (.in0(multiplexer_123_out), .in1(1'b0), .out(S[5]), .sel(Move[4]));
  Multiplexer #(.enable("false")) multiplexer_156 (.in0(multiplexer_124_out), .in1(1'b0), .out(S[4]), .sel(Move[4]));
  Multiplexer #(.enable("false")) multiplexer_157 (.in0(multiplexer_125_out), .in1(1'b0), .out(S[3]), .sel(Move[4]));
  Multiplexer #(.enable("false")) multiplexer_158 (.in0(multiplexer_126_out), .in1(1'b0), .out(S[2]), .sel(Move[4]));
  Multiplexer #(.enable("false")) multiplexer_159 (.in0(multiplexer_127_out), .in1(1'b0), .out(S[1]), .sel(Move[4]));
  Multiplexer #(.enable("false")) multiplexer_160 (.in0(multiplexer_128_out), .in1(1'b0), .out(S[0]), .sel(Move[4]));
endmodule

module deslDir (
  input  [31:0] A,
  input  [4:0] Move,
  output [31:0] S
);

  wire multiplexer_1_out, multiplexer_2_out, multiplexer_3_out, multiplexer_4_out, multiplexer_5_out,
       multiplexer_6_out, multiplexer_7_out, multiplexer_8_out, multiplexer_9_out, multiplexer_10_out,
       multiplexer_11_out, multiplexer_12_out, multiplexer_13_out, multiplexer_14_out, multiplexer_15_out,
       multiplexer_16_out, multiplexer_17_out, multiplexer_18_out, multiplexer_19_out, multiplexer_20_out,
       multiplexer_21_out, multiplexer_22_out, multiplexer_23_out, multiplexer_24_out, multiplexer_25_out,
       multiplexer_26_out, multiplexer_27_out, multiplexer_28_out, multiplexer_29_out, multiplexer_30_out,
       multiplexer_31_out, multiplexer_32_out, multiplexer_33_out, multiplexer_34_out, multiplexer_35_out,
       multiplexer_36_out, multiplexer_37_out, multiplexer_38_out, multiplexer_39_out, multiplexer_40_out,
       multiplexer_41_out, multiplexer_42_out, multiplexer_43_out, multiplexer_44_out, multiplexer_45_out,
       multiplexer_46_out, multiplexer_47_out, multiplexer_48_out, multiplexer_49_out, multiplexer_50_out,
       multiplexer_51_out, multiplexer_52_out, multiplexer_53_out, multiplexer_54_out, multiplexer_55_out,
       multiplexer_56_out, multiplexer_57_out, multiplexer_58_out, multiplexer_59_out, multiplexer_60_out,
       multiplexer_61_out, multiplexer_62_out, multiplexer_63_out, multiplexer_64_out, multiplexer_65_out,
       multiplexer_66_out, multiplexer_67_out, multiplexer_68_out, multiplexer_69_out, multiplexer_70_out,
       multiplexer_71_out, multiplexer_72_out, multiplexer_73_out, multiplexer_74_out, multiplexer_75_out,
       multiplexer_76_out, multiplexer_77_out, multiplexer_78_out, multiplexer_79_out, multiplexer_80_out,
       multiplexer_81_out, multiplexer_82_out, multiplexer_83_out, multiplexer_84_out, multiplexer_85_out,
       multiplexer_86_out, multiplexer_87_out, multiplexer_88_out, multiplexer_89_out, multiplexer_90_out,
       multiplexer_91_out, multiplexer_92_out, multiplexer_93_out, multiplexer_94_out, multiplexer_95_out,
       multiplexer_96_out, multiplexer_97_out, multiplexer_98_out, multiplexer_99_out, multiplexer_100_out,
       multiplexer_101_out, multiplexer_102_out, multiplexer_103_out, multiplexer_104_out,
       multiplexer_105_out, multiplexer_106_out, multiplexer_107_out, multiplexer_108_out,
       multiplexer_109_out, multiplexer_110_out, multiplexer_111_out, multiplexer_112_out,
       multiplexer_113_out, multiplexer_114_out, multiplexer_115_out, multiplexer_116_out,
       multiplexer_117_out, multiplexer_118_out, multiplexer_119_out, multiplexer_120_out,
       multiplexer_121_out, multiplexer_122_out, multiplexer_123_out, multiplexer_124_out,
       multiplexer_125_out, multiplexer_126_out, multiplexer_127_out, multiplexer_128_out;

  Multiplexer #(.enable("false")) multiplexer_1 (.in0(A[0]), .in1(A[1]), .out(multiplexer_1_out), .sel(Move[0]));
  Multiplexer #(.enable("false")) multiplexer_2 (.in0(A[1]), .in1(A[2]), .out(multiplexer_2_out), .sel(Move[0]));
  Multiplexer #(.enable("false")) multiplexer_3 (.in0(A[2]), .in1(A[3]), .out(multiplexer_3_out), .sel(Move[0]));
  Multiplexer #(.enable("false")) multiplexer_4 (.in0(A[3]), .in1(A[4]), .out(multiplexer_4_out), .sel(Move[0]));
  Multiplexer #(.enable("false")) multiplexer_5 (.in0(A[4]), .in1(A[5]), .out(multiplexer_5_out), .sel(Move[0]));
  Multiplexer #(.enable("false")) multiplexer_6 (.in0(A[5]), .in1(A[6]), .out(multiplexer_6_out), .sel(Move[0]));
  Multiplexer #(.enable("false")) multiplexer_7 (.in0(A[6]), .in1(A[7]), .out(multiplexer_7_out), .sel(Move[0]));
  Multiplexer #(.enable("false")) multiplexer_8 (.in0(A[7]), .in1(A[8]), .out(multiplexer_8_out), .sel(Move[0]));
  Multiplexer #(.enable("false")) multiplexer_9 (.in0(A[8]), .in1(A[9]), .out(multiplexer_9_out), .sel(Move[0]));
  Multiplexer #(.enable("false")) multiplexer_10 (.in0(A[9]), .in1(A[10]), .out(multiplexer_10_out), .sel(Move[0]));
  Multiplexer #(.enable("false")) multiplexer_11 (.in0(A[10]), .in1(A[11]), .out(multiplexer_11_out), .sel(Move[0]));
  Multiplexer #(.enable("false")) multiplexer_12 (.in0(A[11]), .in1(A[12]), .out(multiplexer_12_out), .sel(Move[0]));
  Multiplexer #(.enable("false")) multiplexer_13 (.in0(A[12]), .in1(A[13]), .out(multiplexer_13_out), .sel(Move[0]));
  Multiplexer #(.enable("false")) multiplexer_14 (.in0(A[13]), .in1(A[14]), .out(multiplexer_14_out), .sel(Move[0]));
  Multiplexer #(.enable("false")) multiplexer_15 (.in0(A[14]), .in1(A[15]), .out(multiplexer_15_out), .sel(Move[0]));
  Multiplexer #(.enable("false")) multiplexer_16 (.in0(A[15]), .in1(A[16]), .out(multiplexer_16_out), .sel(Move[0]));
  Multiplexer #(.enable("false")) multiplexer_17 (.in0(A[16]), .in1(A[17]), .out(multiplexer_17_out), .sel(Move[0]));
  Multiplexer #(.enable("false")) multiplexer_18 (.in0(A[17]), .in1(A[18]), .out(multiplexer_18_out), .sel(Move[0]));
  Multiplexer #(.enable("false")) multiplexer_19 (.in0(A[18]), .in1(A[19]), .out(multiplexer_19_out), .sel(Move[0]));
  Multiplexer #(.enable("false")) multiplexer_20 (.in0(A[19]), .in1(A[20]), .out(multiplexer_20_out), .sel(Move[0]));
  Multiplexer #(.enable("false")) multiplexer_21 (.in0(A[20]), .in1(A[21]), .out(multiplexer_21_out), .sel(Move[0]));
  Multiplexer #(.enable("false")) multiplexer_22 (.in0(A[21]), .in1(A[22]), .out(multiplexer_22_out), .sel(Move[0]));
  Multiplexer #(.enable("false")) multiplexer_23 (.in0(A[22]), .in1(A[23]), .out(multiplexer_23_out), .sel(Move[0]));
  Multiplexer #(.enable("false")) multiplexer_24 (.in0(A[23]), .in1(A[24]), .out(multiplexer_24_out), .sel(Move[0]));
  Multiplexer #(.enable("false")) multiplexer_25 (.in0(A[24]), .in1(A[25]), .out(multiplexer_25_out), .sel(Move[0]));
  Multiplexer #(.enable("false")) multiplexer_26 (.in0(A[25]), .in1(A[26]), .out(multiplexer_26_out), .sel(Move[0]));
  Multiplexer #(.enable("false")) multiplexer_27 (.in0(A[26]), .in1(A[27]), .out(multiplexer_27_out), .sel(Move[0]));
  Multiplexer #(.enable("false")) multiplexer_28 (.in0(A[27]), .in1(A[28]), .out(multiplexer_28_out), .sel(Move[0]));
  Multiplexer #(.enable("false")) multiplexer_29 (.in0(A[28]), .in1(A[29]), .out(multiplexer_29_out), .sel(Move[0]));
  Multiplexer #(.enable("false")) multiplexer_30 (.in0(A[29]), .in1(A[30]), .out(multiplexer_30_out), .sel(Move[0]));
  Multiplexer #(.enable("false")) multiplexer_31 (.in0(A[30]), .in1(A[31]), .out(multiplexer_31_out), .sel(Move[0]));
  Multiplexer #(.enable("false")) multiplexer_32 (.in0(A[31]), .in1(1'b0), .out(multiplexer_32_out), .sel(Move[0]));
  Multiplexer #(.enable("false")) multiplexer_33 (
    .in0(multiplexer_1_out), .in1(multiplexer_3_out), .out(multiplexer_33_out), .sel(Move[1]));
  Multiplexer #(.enable("false")) multiplexer_34 (
    .in0(multiplexer_2_out), .in1(multiplexer_4_out), .out(multiplexer_34_out), .sel(Move[1]));
  Multiplexer #(.enable("false")) multiplexer_35 (
    .in0(multiplexer_3_out), .in1(multiplexer_5_out), .out(multiplexer_35_out), .sel(Move[1]));
  Multiplexer #(.enable("false")) multiplexer_36 (
    .in0(multiplexer_4_out), .in1(multiplexer_6_out), .out(multiplexer_36_out), .sel(Move[1]));
  Multiplexer #(.enable("false")) multiplexer_37 (
    .in0(multiplexer_5_out), .in1(multiplexer_7_out), .out(multiplexer_37_out), .sel(Move[1]));
  Multiplexer #(.enable("false")) multiplexer_38 (
    .in0(multiplexer_6_out), .in1(multiplexer_8_out), .out(multiplexer_38_out), .sel(Move[1]));
  Multiplexer #(.enable("false")) multiplexer_39 (
    .in0(multiplexer_7_out), .in1(multiplexer_9_out), .out(multiplexer_39_out), .sel(Move[1]));
  Multiplexer #(.enable("false")) multiplexer_40 (
    .in0(multiplexer_8_out), .in1(multiplexer_10_out), .out(multiplexer_40_out), .sel(Move[1]));
  Multiplexer #(.enable("false")) multiplexer_41 (
    .in0(multiplexer_9_out), .in1(multiplexer_11_out), .out(multiplexer_41_out), .sel(Move[1]));
  Multiplexer #(.enable("false")) multiplexer_42 (
    .in0(multiplexer_10_out), .in1(multiplexer_12_out), .out(multiplexer_42_out), .sel(Move[1]));
  Multiplexer #(.enable("false")) multiplexer_43 (
    .in0(multiplexer_11_out), .in1(multiplexer_13_out), .out(multiplexer_43_out), .sel(Move[1]));
  Multiplexer #(.enable("false")) multiplexer_44 (
    .in0(multiplexer_12_out), .in1(multiplexer_14_out), .out(multiplexer_44_out), .sel(Move[1]));
  Multiplexer #(.enable("false")) multiplexer_45 (
    .in0(multiplexer_13_out), .in1(multiplexer_15_out), .out(multiplexer_45_out), .sel(Move[1]));
  Multiplexer #(.enable("false")) multiplexer_46 (
    .in0(multiplexer_14_out), .in1(multiplexer_16_out), .out(multiplexer_46_out), .sel(Move[1]));
  Multiplexer #(.enable("false")) multiplexer_47 (
    .in0(multiplexer_15_out), .in1(multiplexer_17_out), .out(multiplexer_47_out), .sel(Move[1]));
  Multiplexer #(.enable("false")) multiplexer_48 (
    .in0(multiplexer_16_out), .in1(multiplexer_18_out), .out(multiplexer_48_out), .sel(Move[1]));
  Multiplexer #(.enable("false")) multiplexer_49 (
    .in0(multiplexer_17_out), .in1(multiplexer_19_out), .out(multiplexer_49_out), .sel(Move[1]));
  Multiplexer #(.enable("false")) multiplexer_50 (
    .in0(multiplexer_18_out), .in1(multiplexer_20_out), .out(multiplexer_50_out), .sel(Move[1]));
  Multiplexer #(.enable("false")) multiplexer_51 (
    .in0(multiplexer_19_out), .in1(multiplexer_21_out), .out(multiplexer_51_out), .sel(Move[1]));
  Multiplexer #(.enable("false")) multiplexer_52 (
    .in0(multiplexer_20_out), .in1(multiplexer_22_out), .out(multiplexer_52_out), .sel(Move[1]));
  Multiplexer #(.enable("false")) multiplexer_53 (
    .in0(multiplexer_21_out), .in1(multiplexer_23_out), .out(multiplexer_53_out), .sel(Move[1]));
  Multiplexer #(.enable("false")) multiplexer_54 (
    .in0(multiplexer_22_out), .in1(multiplexer_24_out), .out(multiplexer_54_out), .sel(Move[1]));
  Multiplexer #(.enable("false")) multiplexer_55 (
    .in0(multiplexer_23_out), .in1(multiplexer_25_out), .out(multiplexer_55_out), .sel(Move[1]));
  Multiplexer #(.enable("false")) multiplexer_56 (
    .in0(multiplexer_24_out), .in1(multiplexer_26_out), .out(multiplexer_56_out), .sel(Move[1]));
  Multiplexer #(.enable("false")) multiplexer_57 (
    .in0(multiplexer_25_out), .in1(multiplexer_27_out), .out(multiplexer_57_out), .sel(Move[1]));
  Multiplexer #(.enable("false")) multiplexer_58 (
    .in0(multiplexer_26_out), .in1(multiplexer_28_out), .out(multiplexer_58_out), .sel(Move[1]));
  Multiplexer #(.enable("false")) multiplexer_59 (
    .in0(multiplexer_27_out), .in1(multiplexer_29_out), .out(multiplexer_59_out), .sel(Move[1]));
  Multiplexer #(.enable("false")) multiplexer_60 (
    .in0(multiplexer_28_out), .in1(multiplexer_30_out), .out(multiplexer_60_out), .sel(Move[1]));
  Multiplexer #(.enable("false")) multiplexer_61 (
    .in0(multiplexer_29_out), .in1(multiplexer_31_out), .out(multiplexer_61_out), .sel(Move[1]));
  Multiplexer #(.enable("false")) multiplexer_62 (
    .in0(multiplexer_30_out), .in1(multiplexer_32_out), .out(multiplexer_62_out), .sel(Move[1]));
  Multiplexer #(.enable("false")) multiplexer_63 (
    .in0(multiplexer_31_out), .in1(1'b0), .out(multiplexer_63_out), .sel(Move[1]));
  Multiplexer #(.enable("false")) multiplexer_64 (
    .in0(multiplexer_32_out), .in1(1'b0), .out(multiplexer_64_out), .sel(Move[1]));
  Multiplexer #(.enable("false")) multiplexer_65 (
    .in0(multiplexer_33_out), .in1(multiplexer_37_out), .out(multiplexer_65_out), .sel(Move[2]));
  Multiplexer #(.enable("false")) multiplexer_66 (
    .in0(multiplexer_34_out), .in1(multiplexer_38_out), .out(multiplexer_66_out), .sel(Move[2]));
  Multiplexer #(.enable("false")) multiplexer_67 (
    .in0(multiplexer_35_out), .in1(multiplexer_39_out), .out(multiplexer_67_out), .sel(Move[2]));
  Multiplexer #(.enable("false")) multiplexer_68 (
    .in0(multiplexer_36_out), .in1(multiplexer_40_out), .out(multiplexer_68_out), .sel(Move[2]));
  Multiplexer #(.enable("false")) multiplexer_69 (
    .in0(multiplexer_37_out), .in1(multiplexer_41_out), .out(multiplexer_69_out), .sel(Move[2]));
  Multiplexer #(.enable("false")) multiplexer_70 (
    .in0(multiplexer_38_out), .in1(multiplexer_42_out), .out(multiplexer_70_out), .sel(Move[2]));
  Multiplexer #(.enable("false")) multiplexer_71 (
    .in0(multiplexer_39_out), .in1(multiplexer_43_out), .out(multiplexer_71_out), .sel(Move[2]));
  Multiplexer #(.enable("false")) multiplexer_72 (
    .in0(multiplexer_40_out), .in1(multiplexer_44_out), .out(multiplexer_72_out), .sel(Move[2]));
  Multiplexer #(.enable("false")) multiplexer_73 (
    .in0(multiplexer_41_out), .in1(multiplexer_45_out), .out(multiplexer_73_out), .sel(Move[2]));
  Multiplexer #(.enable("false")) multiplexer_74 (
    .in0(multiplexer_42_out), .in1(multiplexer_46_out), .out(multiplexer_74_out), .sel(Move[2]));
  Multiplexer #(.enable("false")) multiplexer_75 (
    .in0(multiplexer_43_out), .in1(multiplexer_47_out), .out(multiplexer_75_out), .sel(Move[2]));
  Multiplexer #(.enable("false")) multiplexer_76 (
    .in0(multiplexer_44_out), .in1(multiplexer_48_out), .out(multiplexer_76_out), .sel(Move[2]));
  Multiplexer #(.enable("false")) multiplexer_77 (
    .in0(multiplexer_45_out), .in1(multiplexer_49_out), .out(multiplexer_77_out), .sel(Move[2]));
  Multiplexer #(.enable("false")) multiplexer_78 (
    .in0(multiplexer_46_out), .in1(multiplexer_50_out), .out(multiplexer_78_out), .sel(Move[2]));
  Multiplexer #(.enable("false")) multiplexer_79 (
    .in0(multiplexer_47_out), .in1(multiplexer_51_out), .out(multiplexer_79_out), .sel(Move[2]));
  Multiplexer #(.enable("false")) multiplexer_80 (
    .in0(multiplexer_48_out), .in1(multiplexer_52_out), .out(multiplexer_80_out), .sel(Move[2]));
  Multiplexer #(.enable("false")) multiplexer_81 (
    .in0(multiplexer_49_out), .in1(multiplexer_53_out), .out(multiplexer_81_out), .sel(Move[2]));
  Multiplexer #(.enable("false")) multiplexer_82 (
    .in0(multiplexer_50_out), .in1(multiplexer_54_out), .out(multiplexer_82_out), .sel(Move[2]));
  Multiplexer #(.enable("false")) multiplexer_83 (
    .in0(multiplexer_51_out), .in1(multiplexer_55_out), .out(multiplexer_83_out), .sel(Move[2]));
  Multiplexer #(.enable("false")) multiplexer_84 (
    .in0(multiplexer_52_out), .in1(multiplexer_56_out), .out(multiplexer_84_out), .sel(Move[2]));
  Multiplexer #(.enable("false")) multiplexer_85 (
    .in0(multiplexer_53_out), .in1(multiplexer_57_out), .out(multiplexer_85_out), .sel(Move[2]));
  Multiplexer #(.enable("false")) multiplexer_86 (
    .in0(multiplexer_54_out), .in1(multiplexer_58_out), .out(multiplexer_86_out), .sel(Move[2]));
  Multiplexer #(.enable("false")) multiplexer_87 (
    .in0(multiplexer_55_out), .in1(multiplexer_59_out), .out(multiplexer_87_out), .sel(Move[2]));
  Multiplexer #(.enable("false")) multiplexer_88 (
    .in0(multiplexer_56_out), .in1(multiplexer_60_out), .out(multiplexer_88_out), .sel(Move[2]));
  Multiplexer #(.enable("false")) multiplexer_89 (
    .in0(multiplexer_57_out), .in1(multiplexer_61_out), .out(multiplexer_89_out), .sel(Move[2]));
  Multiplexer #(.enable("false")) multiplexer_90 (
    .in0(multiplexer_58_out), .in1(multiplexer_62_out), .out(multiplexer_90_out), .sel(Move[2]));
  Multiplexer #(.enable("false")) multiplexer_91 (
    .in0(multiplexer_59_out), .in1(multiplexer_63_out), .out(multiplexer_91_out), .sel(Move[2]));
  Multiplexer #(.enable("false")) multiplexer_92 (
    .in0(multiplexer_60_out), .in1(multiplexer_64_out), .out(multiplexer_92_out), .sel(Move[2]));
  Multiplexer #(.enable("false")) multiplexer_93 (
    .in0(multiplexer_61_out), .in1(1'b0), .out(multiplexer_93_out), .sel(Move[2]));
  Multiplexer #(.enable("false")) multiplexer_94 (
    .in0(multiplexer_62_out), .in1(1'b0), .out(multiplexer_94_out), .sel(Move[2]));
  Multiplexer #(.enable("false")) multiplexer_95 (
    .in0(multiplexer_63_out), .in1(1'b0), .out(multiplexer_95_out), .sel(Move[2]));
  Multiplexer #(.enable("false")) multiplexer_96 (
    .in0(multiplexer_64_out), .in1(1'b0), .out(multiplexer_96_out), .sel(Move[2]));
  Multiplexer #(.enable("false")) multiplexer_97 (
    .in0(multiplexer_65_out), .in1(multiplexer_73_out), .out(multiplexer_97_out), .sel(Move[3]));
  Multiplexer #(.enable("false")) multiplexer_98 (
    .in0(multiplexer_66_out), .in1(multiplexer_74_out), .out(multiplexer_98_out), .sel(Move[3]));
  Multiplexer #(.enable("false")) multiplexer_99 (
    .in0(multiplexer_67_out), .in1(multiplexer_75_out), .out(multiplexer_99_out), .sel(Move[3]));
  Multiplexer #(.enable("false")) multiplexer_100 (
    .in0(multiplexer_68_out), .in1(multiplexer_76_out), .out(multiplexer_100_out), .sel(Move[3]));
  Multiplexer #(.enable("false")) multiplexer_101 (
    .in0(multiplexer_69_out), .in1(multiplexer_77_out), .out(multiplexer_101_out), .sel(Move[3]));
  Multiplexer #(.enable("false")) multiplexer_102 (
    .in0(multiplexer_70_out), .in1(multiplexer_78_out), .out(multiplexer_102_out), .sel(Move[3]));
  Multiplexer #(.enable("false")) multiplexer_103 (
    .in0(multiplexer_71_out), .in1(multiplexer_79_out), .out(multiplexer_103_out), .sel(Move[3]));
  Multiplexer #(.enable("false")) multiplexer_104 (
    .in0(multiplexer_72_out), .in1(multiplexer_80_out), .out(multiplexer_104_out), .sel(Move[3]));
  Multiplexer #(.enable("false")) multiplexer_105 (
    .in0(multiplexer_73_out), .in1(multiplexer_81_out), .out(multiplexer_105_out), .sel(Move[3]));
  Multiplexer #(.enable("false")) multiplexer_106 (
    .in0(multiplexer_74_out), .in1(multiplexer_82_out), .out(multiplexer_106_out), .sel(Move[3]));
  Multiplexer #(.enable("false")) multiplexer_107 (
    .in0(multiplexer_75_out), .in1(multiplexer_83_out), .out(multiplexer_107_out), .sel(Move[3]));
  Multiplexer #(.enable("false")) multiplexer_108 (
    .in0(multiplexer_76_out), .in1(multiplexer_84_out), .out(multiplexer_108_out), .sel(Move[3]));
  Multiplexer #(.enable("false")) multiplexer_109 (
    .in0(multiplexer_77_out), .in1(multiplexer_85_out), .out(multiplexer_109_out), .sel(Move[3]));
  Multiplexer #(.enable("false")) multiplexer_110 (
    .in0(multiplexer_78_out), .in1(multiplexer_86_out), .out(multiplexer_110_out), .sel(Move[3]));
  Multiplexer #(.enable("false")) multiplexer_111 (
    .in0(multiplexer_79_out), .in1(multiplexer_87_out), .out(multiplexer_111_out), .sel(Move[3]));
  Multiplexer #(.enable("false")) multiplexer_112 (
    .in0(multiplexer_80_out), .in1(multiplexer_88_out), .out(multiplexer_112_out), .sel(Move[3]));
  Multiplexer #(.enable("false")) multiplexer_113 (
    .in0(multiplexer_81_out), .in1(multiplexer_89_out), .out(multiplexer_113_out), .sel(Move[3]));
  Multiplexer #(.enable("false")) multiplexer_114 (
    .in0(multiplexer_82_out), .in1(multiplexer_90_out), .out(multiplexer_114_out), .sel(Move[3]));
  Multiplexer #(.enable("false")) multiplexer_115 (
    .in0(multiplexer_83_out), .in1(multiplexer_91_out), .out(multiplexer_115_out), .sel(Move[3]));
  Multiplexer #(.enable("false")) multiplexer_116 (
    .in0(multiplexer_84_out), .in1(multiplexer_92_out), .out(multiplexer_116_out), .sel(Move[3]));
  Multiplexer #(.enable("false")) multiplexer_117 (
    .in0(multiplexer_85_out), .in1(multiplexer_93_out), .out(multiplexer_117_out), .sel(Move[3]));
  Multiplexer #(.enable("false")) multiplexer_118 (
    .in0(multiplexer_86_out), .in1(multiplexer_94_out), .out(multiplexer_118_out), .sel(Move[3]));
  Multiplexer #(.enable("false")) multiplexer_119 (
    .in0(multiplexer_87_out), .in1(multiplexer_95_out), .out(multiplexer_119_out), .sel(Move[3]));
  Multiplexer #(.enable("false")) multiplexer_120 (
    .in0(multiplexer_88_out), .in1(multiplexer_96_out), .out(multiplexer_120_out), .sel(Move[3]));
  Multiplexer #(.enable("false")) multiplexer_121 (
    .in0(multiplexer_89_out), .in1(1'b0), .out(multiplexer_121_out), .sel(Move[3]));
  Multiplexer #(.enable("false")) multiplexer_122 (
    .in0(multiplexer_90_out), .in1(1'b0), .out(multiplexer_122_out), .sel(Move[3]));
  Multiplexer #(.enable("false")) multiplexer_123 (
    .in0(multiplexer_91_out), .in1(1'b0), .out(multiplexer_123_out), .sel(Move[3]));
  Multiplexer #(.enable("false")) multiplexer_124 (
    .in0(multiplexer_92_out), .in1(1'b0), .out(multiplexer_124_out), .sel(Move[3]));
  Multiplexer #(.enable("false")) multiplexer_125 (
    .in0(multiplexer_93_out), .in1(1'b0), .out(multiplexer_125_out), .sel(Move[3]));
  Multiplexer #(.enable("false")) multiplexer_126 (
    .in0(multiplexer_94_out), .in1(1'b0), .out(multiplexer_126_out), .sel(Move[3]));
  Multiplexer #(.enable("false")) multiplexer_127 (
    .in0(multiplexer_95_out), .in1(1'b0), .out(multiplexer_127_out), .sel(Move[3]));
  Multiplexer #(.enable("false")) multiplexer_128 (
    .in0(multiplexer_96_out), .in1(1'b0), .out(multiplexer_128_out), .sel(Move[3]));
  Multiplexer #(.enable("false")) multiplexer_129 (
    .in0(multiplexer_97_out), .in1(multiplexer_113_out), .out(S[0]), .sel(Move[4]));
  Multiplexer #(.enable("false")) multiplexer_130 (
    .in0(multiplexer_98_out), .in1(multiplexer_114_out), .out(S[1]), .sel(Move[4]));
  Multiplexer #(.enable("false")) multiplexer_131 (
    .in0(multiplexer_99_out), .in1(multiplexer_115_out), .out(S[2]), .sel(Move[4]));
  Multiplexer #(.enable("false")) multiplexer_132 (
    .in0(multiplexer_100_out), .in1(multiplexer_116_out), .out(S[3]), .sel(Move[4]));
  Multiplexer #(.enable("false")) multiplexer_133 (
    .in0(multiplexer_101_out), .in1(multiplexer_117_out), .out(S[4]), .sel(Move[4]));
  Multiplexer #(.enable("false")) multiplexer_134 (
    .in0(multiplexer_102_out), .in1(multiplexer_118_out), .out(S[5]), .sel(Move[4]));
  Multiplexer #(.enable("false")) multiplexer_135 (
    .in0(multiplexer_103_out), .in1(multiplexer_119_out), .out(S[6]), .sel(Move[4]));
  Multiplexer #(.enable("false")) multiplexer_136 (
    .in0(multiplexer_104_out), .in1(multiplexer_120_out), .out(S[7]), .sel(Move[4]));
  Multiplexer #(.enable("false")) multiplexer_137 (
    .in0(multiplexer_105_out), .in1(multiplexer_121_out), .out(S[8]), .sel(Move[4]));
  Multiplexer #(.enable("false")) multiplexer_138 (
    .in0(multiplexer_106_out), .in1(multiplexer_122_out), .out(S[9]), .sel(Move[4]));
  Multiplexer #(.enable("false")) multiplexer_139 (
    .in0(multiplexer_107_out), .in1(multiplexer_123_out), .out(S[10]), .sel(Move[4]));
  Multiplexer #(.enable("false")) multiplexer_140 (
    .in0(multiplexer_108_out), .in1(multiplexer_124_out), .out(S[11]), .sel(Move[4]));
  Multiplexer #(.enable("false")) multiplexer_141 (
    .in0(multiplexer_109_out), .in1(multiplexer_125_out), .out(S[12]), .sel(Move[4]));
  Multiplexer #(.enable("false")) multiplexer_142 (
    .in0(multiplexer_110_out), .in1(multiplexer_126_out), .out(S[13]), .sel(Move[4]));
  Multiplexer #(.enable("false")) multiplexer_143 (
    .in0(multiplexer_111_out), .in1(multiplexer_127_out), .out(S[14]), .sel(Move[4]));
  Multiplexer #(.enable("false")) multiplexer_144 (
    .in0(multiplexer_112_out), .in1(multiplexer_128_out), .out(S[15]), .sel(Move[4]));
  Multiplexer #(.enable("false")) multiplexer_145 (.in0(multiplexer_113_out), .in1(1'b0), .out(S[16]), .sel(Move[4]));
  Multiplexer #(.enable("false")) multiplexer_146 (.in0(multiplexer_114_out), .in1(1'b0), .out(S[17]), .sel(Move[4]));
  Multiplexer #(.enable("false")) multiplexer_147 (.in0(multiplexer_115_out), .in1(1'b0), .out(S[18]), .sel(Move[4]));
  Multiplexer #(.enable("false")) multiplexer_148 (.in0(multiplexer_116_out), .in1(1'b0), .out(S[19]), .sel(Move[4]));
  Multiplexer #(.enable("false")) multiplexer_149 (.in0(multiplexer_117_out), .in1(1'b0), .out(S[20]), .sel(Move[4]));
  Multiplexer #(.enable("false")) multiplexer_150 (.in0(multiplexer_118_out), .in1(1'b0), .out(S[21]), .sel(Move[4]));
  Multiplexer #(.enable("false")) multiplexer_151 (.in0(multiplexer_119_out), .in1(1'b0), .out(S[22]), .sel(Move[4]));
  Multiplexer #(.enable("false")) multiplexer_152 (.in0(multiplexer_120_out), .in1(1'b0), .out(S[23]), .sel(Move[4]));
  Multiplexer #(.enable("false")) multiplexer_153 (.in0(multiplexer_121_out), .in1(1'b0), .out(S[24]), .sel(Move[4]));
  Multiplexer #(.enable("false")) multiplexer_154 (.in0(multiplexer_122_out), .in1(1'b0), .out(S[25]), .sel(Move[4]));
  Multiplexer #(.enable("false")) multiplexer_155 (.in0(multiplexer_123_out), .in1(1'b0), .out(S[26]), .sel(Move[4]));
  Multiplexer #(.enable("false")) multiplexer_156 (.in0(multiplexer_124_out), .in1(1'b0), .out(S[27]), .sel(Move[4]));
  Multiplexer #(.enable("false")) multiplexer_157 (.in0(multiplexer_125_out), .in1(1'b0), .out(S[28]), .sel(Move[4]));
  Multiplexer #(.enable("false")) multiplexer_158 (.in0(multiplexer_126_out), .in1(1'b0), .out(S[29]), .sel(Move[4]));
  Multiplexer #(.enable("false")) multiplexer_159 (.in0(multiplexer_127_out), .in1(1'b0), .out(S[30]), .sel(Move[4]));
  Multiplexer #(.enable("false")) multiplexer_160 (.in0(multiplexer_128_out), .in1(1'b0), .out(S[31]), .sel(Move[4]));
endmodule

module deslDirArt (
  input  [31:0] A,
  input  [4:0] Move,
  output [31:0] S
);

  wire multiplexer_1_out, multiplexer_2_out, multiplexer_3_out, multiplexer_4_out, multiplexer_5_out,
       multiplexer_6_out, multiplexer_7_out, multiplexer_8_out, multiplexer_9_out, multiplexer_10_out,
       multiplexer_11_out, multiplexer_12_out, multiplexer_13_out, multiplexer_14_out, multiplexer_15_out,
       multiplexer_16_out, multiplexer_17_out, multiplexer_18_out, multiplexer_19_out, multiplexer_20_out,
       multiplexer_21_out, multiplexer_22_out, multiplexer_23_out, multiplexer_24_out, multiplexer_25_out,
       multiplexer_26_out, multiplexer_27_out, multiplexer_28_out, multiplexer_29_out, multiplexer_30_out,
       multiplexer_31_out, multiplexer_32_out, multiplexer_33_out, multiplexer_34_out, multiplexer_35_out,
       multiplexer_36_out, multiplexer_37_out, multiplexer_38_out, multiplexer_39_out, multiplexer_40_out,
       multiplexer_41_out, multiplexer_42_out, multiplexer_43_out, multiplexer_44_out, multiplexer_45_out,
       multiplexer_46_out, multiplexer_47_out, multiplexer_48_out, multiplexer_49_out, multiplexer_50_out,
       multiplexer_51_out, multiplexer_52_out, multiplexer_53_out, multiplexer_54_out, multiplexer_55_out,
       multiplexer_56_out, multiplexer_57_out, multiplexer_58_out, multiplexer_59_out, multiplexer_60_out,
       multiplexer_61_out, multiplexer_62_out, multiplexer_63_out, multiplexer_64_out, multiplexer_65_out,
       multiplexer_66_out, multiplexer_67_out, multiplexer_68_out, multiplexer_69_out, multiplexer_70_out,
       multiplexer_71_out, multiplexer_72_out, multiplexer_73_out, multiplexer_74_out, multiplexer_75_out,
       multiplexer_76_out, multiplexer_77_out, multiplexer_78_out, multiplexer_79_out, multiplexer_80_out,
       multiplexer_81_out, multiplexer_82_out, multiplexer_83_out, multiplexer_84_out, multiplexer_85_out,
       multiplexer_86_out, multiplexer_87_out, multiplexer_88_out, multiplexer_89_out, multiplexer_90_out,
       multiplexer_91_out, multiplexer_92_out, multiplexer_93_out, multiplexer_94_out, multiplexer_95_out,
       multiplexer_96_out, multiplexer_97_out, multiplexer_98_out, multiplexer_99_out, multiplexer_100_out,
       multiplexer_101_out, multiplexer_102_out, multiplexer_103_out, multiplexer_104_out,
       multiplexer_105_out, multiplexer_106_out, multiplexer_107_out, multiplexer_108_out,
       multiplexer_109_out, multiplexer_110_out, multiplexer_111_out, multiplexer_112_out,
       multiplexer_113_out, multiplexer_114_out, multiplexer_115_out, multiplexer_116_out,
       multiplexer_117_out, multiplexer_118_out, multiplexer_119_out, multiplexer_120_out,
       multiplexer_121_out, multiplexer_122_out, multiplexer_123_out, multiplexer_124_out;

  Multiplexer #(.enable("false")) multiplexer_1 (.in0(A[0]), .in1(A[1]), .out(multiplexer_1_out), .sel(Move[0]));
  Multiplexer #(.enable("false")) multiplexer_2 (.in0(A[1]), .in1(A[2]), .out(multiplexer_2_out), .sel(Move[0]));
  Multiplexer #(.enable("false")) multiplexer_3 (.in0(A[2]), .in1(A[3]), .out(multiplexer_3_out), .sel(Move[0]));
  Multiplexer #(.enable("false")) multiplexer_4 (.in0(A[3]), .in1(A[4]), .out(multiplexer_4_out), .sel(Move[0]));
  Multiplexer #(.enable("false")) multiplexer_5 (.in0(A[4]), .in1(A[5]), .out(multiplexer_5_out), .sel(Move[0]));
  Multiplexer #(.enable("false")) multiplexer_6 (.in0(A[5]), .in1(A[6]), .out(multiplexer_6_out), .sel(Move[0]));
  Multiplexer #(.enable("false")) multiplexer_7 (.in0(A[6]), .in1(A[7]), .out(multiplexer_7_out), .sel(Move[0]));
  Multiplexer #(.enable("false")) multiplexer_8 (.in0(A[7]), .in1(A[8]), .out(multiplexer_8_out), .sel(Move[0]));
  Multiplexer #(.enable("false")) multiplexer_9 (.in0(A[8]), .in1(A[9]), .out(multiplexer_9_out), .sel(Move[0]));
  Multiplexer #(.enable("false")) multiplexer_10 (.in0(A[9]), .in1(A[10]), .out(multiplexer_10_out), .sel(Move[0]));
  Multiplexer #(.enable("false")) multiplexer_11 (.in0(A[10]), .in1(A[11]), .out(multiplexer_11_out), .sel(Move[0]));
  Multiplexer #(.enable("false")) multiplexer_12 (.in0(A[11]), .in1(A[12]), .out(multiplexer_12_out), .sel(Move[0]));
  Multiplexer #(.enable("false")) multiplexer_13 (.in0(A[12]), .in1(A[13]), .out(multiplexer_13_out), .sel(Move[0]));
  Multiplexer #(.enable("false")) multiplexer_14 (.in0(A[13]), .in1(A[14]), .out(multiplexer_14_out), .sel(Move[0]));
  Multiplexer #(.enable("false")) multiplexer_15 (.in0(A[14]), .in1(A[15]), .out(multiplexer_15_out), .sel(Move[0]));
  Multiplexer #(.enable("false")) multiplexer_16 (.in0(A[15]), .in1(A[16]), .out(multiplexer_16_out), .sel(Move[0]));
  Multiplexer #(.enable("false")) multiplexer_17 (.in0(A[16]), .in1(A[17]), .out(multiplexer_17_out), .sel(Move[0]));
  Multiplexer #(.enable("false")) multiplexer_18 (.in0(A[17]), .in1(A[18]), .out(multiplexer_18_out), .sel(Move[0]));
  Multiplexer #(.enable("false")) multiplexer_19 (.in0(A[18]), .in1(A[19]), .out(multiplexer_19_out), .sel(Move[0]));
  Multiplexer #(.enable("false")) multiplexer_20 (.in0(A[19]), .in1(A[20]), .out(multiplexer_20_out), .sel(Move[0]));
  Multiplexer #(.enable("false")) multiplexer_21 (.in0(A[20]), .in1(A[21]), .out(multiplexer_21_out), .sel(Move[0]));
  Multiplexer #(.enable("false")) multiplexer_22 (.in0(A[21]), .in1(A[22]), .out(multiplexer_22_out), .sel(Move[0]));
  Multiplexer #(.enable("false")) multiplexer_23 (.in0(A[22]), .in1(A[23]), .out(multiplexer_23_out), .sel(Move[0]));
  Multiplexer #(.enable("false")) multiplexer_24 (.in0(A[23]), .in1(A[24]), .out(multiplexer_24_out), .sel(Move[0]));
  Multiplexer #(.enable("false")) multiplexer_25 (.in0(A[24]), .in1(A[25]), .out(multiplexer_25_out), .sel(Move[0]));
  Multiplexer #(.enable("false")) multiplexer_26 (.in0(A[25]), .in1(A[26]), .out(multiplexer_26_out), .sel(Move[0]));
  Multiplexer #(.enable("false")) multiplexer_27 (.in0(A[26]), .in1(A[27]), .out(multiplexer_27_out), .sel(Move[0]));
  Multiplexer #(.enable("false")) multiplexer_28 (.in0(A[27]), .in1(A[28]), .out(multiplexer_28_out), .sel(Move[0]));
  Multiplexer #(.enable("false")) multiplexer_29 (.in0(A[28]), .in1(A[29]), .out(multiplexer_29_out), .sel(Move[0]));
  Multiplexer #(.enable("false")) multiplexer_30 (.in0(A[29]), .in1(A[30]), .out(multiplexer_30_out), .sel(Move[0]));
  Multiplexer #(.enable("false")) multiplexer_31 (.in0(A[30]), .in1(A[31]), .out(multiplexer_31_out), .sel(Move[0]));
  Multiplexer #(.enable("false")) multiplexer_32 (
    .in0(multiplexer_1_out), .in1(multiplexer_3_out), .out(multiplexer_32_out), .sel(Move[1]));
  Multiplexer #(.enable("false")) multiplexer_33 (
    .in0(multiplexer_2_out), .in1(multiplexer_4_out), .out(multiplexer_33_out), .sel(Move[1]));
  Multiplexer #(.enable("false")) multiplexer_34 (
    .in0(multiplexer_3_out), .in1(multiplexer_5_out), .out(multiplexer_34_out), .sel(Move[1]));
  Multiplexer #(.enable("false")) multiplexer_35 (
    .in0(multiplexer_4_out), .in1(multiplexer_6_out), .out(multiplexer_35_out), .sel(Move[1]));
  Multiplexer #(.enable("false")) multiplexer_36 (
    .in0(multiplexer_5_out), .in1(multiplexer_7_out), .out(multiplexer_36_out), .sel(Move[1]));
  Multiplexer #(.enable("false")) multiplexer_37 (
    .in0(multiplexer_6_out), .in1(multiplexer_8_out), .out(multiplexer_37_out), .sel(Move[1]));
  Multiplexer #(.enable("false")) multiplexer_38 (
    .in0(multiplexer_7_out), .in1(multiplexer_9_out), .out(multiplexer_38_out), .sel(Move[1]));
  Multiplexer #(.enable("false")) multiplexer_39 (
    .in0(multiplexer_8_out), .in1(multiplexer_10_out), .out(multiplexer_39_out), .sel(Move[1]));
  Multiplexer #(.enable("false")) multiplexer_40 (
    .in0(multiplexer_9_out), .in1(multiplexer_11_out), .out(multiplexer_40_out), .sel(Move[1]));
  Multiplexer #(.enable("false")) multiplexer_41 (
    .in0(multiplexer_10_out), .in1(multiplexer_12_out), .out(multiplexer_41_out), .sel(Move[1]));
  Multiplexer #(.enable("false")) multiplexer_42 (
    .in0(multiplexer_11_out), .in1(multiplexer_13_out), .out(multiplexer_42_out), .sel(Move[1]));
  Multiplexer #(.enable("false")) multiplexer_43 (
    .in0(multiplexer_12_out), .in1(multiplexer_14_out), .out(multiplexer_43_out), .sel(Move[1]));
  Multiplexer #(.enable("false")) multiplexer_44 (
    .in0(multiplexer_13_out), .in1(multiplexer_15_out), .out(multiplexer_44_out), .sel(Move[1]));
  Multiplexer #(.enable("false")) multiplexer_45 (
    .in0(multiplexer_14_out), .in1(multiplexer_16_out), .out(multiplexer_45_out), .sel(Move[1]));
  Multiplexer #(.enable("false")) multiplexer_46 (
    .in0(multiplexer_15_out), .in1(multiplexer_17_out), .out(multiplexer_46_out), .sel(Move[1]));
  Multiplexer #(.enable("false")) multiplexer_47 (
    .in0(multiplexer_16_out), .in1(multiplexer_18_out), .out(multiplexer_47_out), .sel(Move[1]));
  Multiplexer #(.enable("false")) multiplexer_48 (
    .in0(multiplexer_17_out), .in1(multiplexer_19_out), .out(multiplexer_48_out), .sel(Move[1]));
  Multiplexer #(.enable("false")) multiplexer_49 (
    .in0(multiplexer_18_out), .in1(multiplexer_20_out), .out(multiplexer_49_out), .sel(Move[1]));
  Multiplexer #(.enable("false")) multiplexer_50 (
    .in0(multiplexer_19_out), .in1(multiplexer_21_out), .out(multiplexer_50_out), .sel(Move[1]));
  Multiplexer #(.enable("false")) multiplexer_51 (
    .in0(multiplexer_20_out), .in1(multiplexer_22_out), .out(multiplexer_51_out), .sel(Move[1]));
  Multiplexer #(.enable("false")) multiplexer_52 (
    .in0(multiplexer_21_out), .in1(multiplexer_23_out), .out(multiplexer_52_out), .sel(Move[1]));
  Multiplexer #(.enable("false")) multiplexer_53 (
    .in0(multiplexer_22_out), .in1(multiplexer_24_out), .out(multiplexer_53_out), .sel(Move[1]));
  Multiplexer #(.enable("false")) multiplexer_54 (
    .in0(multiplexer_23_out), .in1(multiplexer_25_out), .out(multiplexer_54_out), .sel(Move[1]));
  Multiplexer #(.enable("false")) multiplexer_55 (
    .in0(multiplexer_24_out), .in1(multiplexer_26_out), .out(multiplexer_55_out), .sel(Move[1]));
  Multiplexer #(.enable("false")) multiplexer_56 (
    .in0(multiplexer_25_out), .in1(multiplexer_27_out), .out(multiplexer_56_out), .sel(Move[1]));
  Multiplexer #(.enable("false")) multiplexer_57 (
    .in0(multiplexer_26_out), .in1(multiplexer_28_out), .out(multiplexer_57_out), .sel(Move[1]));
  Multiplexer #(.enable("false")) multiplexer_58 (
    .in0(multiplexer_27_out), .in1(multiplexer_29_out), .out(multiplexer_58_out), .sel(Move[1]));
  Multiplexer #(.enable("false")) multiplexer_59 (
    .in0(multiplexer_28_out), .in1(multiplexer_30_out), .out(multiplexer_59_out), .sel(Move[1]));
  Multiplexer #(.enable("false")) multiplexer_60 (
    .in0(multiplexer_29_out), .in1(multiplexer_31_out), .out(multiplexer_60_out), .sel(Move[1]));
  Multiplexer #(.enable("false")) multiplexer_61 (
    .in0(multiplexer_30_out), .in1(A[31]), .out(multiplexer_61_out), .sel(Move[1]));
  Multiplexer #(.enable("false")) multiplexer_62 (
    .in0(multiplexer_31_out), .in1(A[31]), .out(multiplexer_62_out), .sel(Move[1]));
  Multiplexer #(.enable("false")) multiplexer_63 (
    .in0(multiplexer_32_out), .in1(multiplexer_36_out), .out(multiplexer_63_out), .sel(Move[2]));
  Multiplexer #(.enable("false")) multiplexer_64 (
    .in0(multiplexer_33_out), .in1(multiplexer_37_out), .out(multiplexer_64_out), .sel(Move[2]));
  Multiplexer #(.enable("false")) multiplexer_65 (
    .in0(multiplexer_34_out), .in1(multiplexer_38_out), .out(multiplexer_65_out), .sel(Move[2]));
  Multiplexer #(.enable("false")) multiplexer_66 (
    .in0(multiplexer_35_out), .in1(multiplexer_39_out), .out(multiplexer_66_out), .sel(Move[2]));
  Multiplexer #(.enable("false")) multiplexer_67 (
    .in0(multiplexer_36_out), .in1(multiplexer_40_out), .out(multiplexer_67_out), .sel(Move[2]));
  Multiplexer #(.enable("false")) multiplexer_68 (
    .in0(multiplexer_37_out), .in1(multiplexer_41_out), .out(multiplexer_68_out), .sel(Move[2]));
  Multiplexer #(.enable("false")) multiplexer_69 (
    .in0(multiplexer_38_out), .in1(multiplexer_42_out), .out(multiplexer_69_out), .sel(Move[2]));
  Multiplexer #(.enable("false")) multiplexer_70 (
    .in0(multiplexer_39_out), .in1(multiplexer_43_out), .out(multiplexer_70_out), .sel(Move[2]));
  Multiplexer #(.enable("false")) multiplexer_71 (
    .in0(multiplexer_40_out), .in1(multiplexer_44_out), .out(multiplexer_71_out), .sel(Move[2]));
  Multiplexer #(.enable("false")) multiplexer_72 (
    .in0(multiplexer_41_out), .in1(multiplexer_45_out), .out(multiplexer_72_out), .sel(Move[2]));
  Multiplexer #(.enable("false")) multiplexer_73 (
    .in0(multiplexer_42_out), .in1(multiplexer_46_out), .out(multiplexer_73_out), .sel(Move[2]));
  Multiplexer #(.enable("false")) multiplexer_74 (
    .in0(multiplexer_43_out), .in1(multiplexer_47_out), .out(multiplexer_74_out), .sel(Move[2]));
  Multiplexer #(.enable("false")) multiplexer_75 (
    .in0(multiplexer_44_out), .in1(multiplexer_48_out), .out(multiplexer_75_out), .sel(Move[2]));
  Multiplexer #(.enable("false")) multiplexer_76 (
    .in0(multiplexer_45_out), .in1(multiplexer_49_out), .out(multiplexer_76_out), .sel(Move[2]));
  Multiplexer #(.enable("false")) multiplexer_77 (
    .in0(multiplexer_46_out), .in1(multiplexer_50_out), .out(multiplexer_77_out), .sel(Move[2]));
  Multiplexer #(.enable("false")) multiplexer_78 (
    .in0(multiplexer_47_out), .in1(multiplexer_51_out), .out(multiplexer_78_out), .sel(Move[2]));
  Multiplexer #(.enable("false")) multiplexer_79 (
    .in0(multiplexer_48_out), .in1(multiplexer_52_out), .out(multiplexer_79_out), .sel(Move[2]));
  Multiplexer #(.enable("false")) multiplexer_80 (
    .in0(multiplexer_49_out), .in1(multiplexer_53_out), .out(multiplexer_80_out), .sel(Move[2]));
  Multiplexer #(.enable("false")) multiplexer_81 (
    .in0(multiplexer_50_out), .in1(multiplexer_54_out), .out(multiplexer_81_out), .sel(Move[2]));
  Multiplexer #(.enable("false")) multiplexer_82 (
    .in0(multiplexer_51_out), .in1(multiplexer_55_out), .out(multiplexer_82_out), .sel(Move[2]));
  Multiplexer #(.enable("false")) multiplexer_83 (
    .in0(multiplexer_52_out), .in1(multiplexer_56_out), .out(multiplexer_83_out), .sel(Move[2]));
  Multiplexer #(.enable("false")) multiplexer_84 (
    .in0(multiplexer_53_out), .in1(multiplexer_57_out), .out(multiplexer_84_out), .sel(Move[2]));
  Multiplexer #(.enable("false")) multiplexer_85 (
    .in0(multiplexer_54_out), .in1(multiplexer_58_out), .out(multiplexer_85_out), .sel(Move[2]));
  Multiplexer #(.enable("false")) multiplexer_86 (
    .in0(multiplexer_55_out), .in1(multiplexer_59_out), .out(multiplexer_86_out), .sel(Move[2]));
  Multiplexer #(.enable("false")) multiplexer_87 (
    .in0(multiplexer_56_out), .in1(multiplexer_60_out), .out(multiplexer_87_out), .sel(Move[2]));
  Multiplexer #(.enable("false")) multiplexer_88 (
    .in0(multiplexer_57_out), .in1(multiplexer_61_out), .out(multiplexer_88_out), .sel(Move[2]));
  Multiplexer #(.enable("false")) multiplexer_89 (
    .in0(multiplexer_58_out), .in1(multiplexer_62_out), .out(multiplexer_89_out), .sel(Move[2]));
  Multiplexer #(.enable("false")) multiplexer_90 (
    .in0(multiplexer_59_out), .in1(A[31]), .out(multiplexer_90_out), .sel(Move[2]));
  Multiplexer #(.enable("false")) multiplexer_91 (
    .in0(multiplexer_60_out), .in1(A[31]), .out(multiplexer_91_out), .sel(Move[2]));
  Multiplexer #(.enable("false")) multiplexer_92 (
    .in0(multiplexer_61_out), .in1(A[31]), .out(multiplexer_92_out), .sel(Move[2]));
  Multiplexer #(.enable("false")) multiplexer_93 (
    .in0(multiplexer_62_out), .in1(A[31]), .out(multiplexer_93_out), .sel(Move[2]));
  Multiplexer #(.enable("false")) multiplexer_94 (
    .in0(multiplexer_63_out), .in1(multiplexer_71_out), .out(multiplexer_94_out), .sel(Move[3]));
  Multiplexer #(.enable("false")) multiplexer_95 (
    .in0(multiplexer_64_out), .in1(multiplexer_72_out), .out(multiplexer_95_out), .sel(Move[3]));
  Multiplexer #(.enable("false")) multiplexer_96 (
    .in0(multiplexer_65_out), .in1(multiplexer_73_out), .out(multiplexer_96_out), .sel(Move[3]));
  Multiplexer #(.enable("false")) multiplexer_97 (
    .in0(multiplexer_66_out), .in1(multiplexer_74_out), .out(multiplexer_97_out), .sel(Move[3]));
  Multiplexer #(.enable("false")) multiplexer_98 (
    .in0(multiplexer_67_out), .in1(multiplexer_75_out), .out(multiplexer_98_out), .sel(Move[3]));
  Multiplexer #(.enable("false")) multiplexer_99 (
    .in0(multiplexer_68_out), .in1(multiplexer_76_out), .out(multiplexer_99_out), .sel(Move[3]));
  Multiplexer #(.enable("false")) multiplexer_100 (
    .in0(multiplexer_69_out), .in1(multiplexer_77_out), .out(multiplexer_100_out), .sel(Move[3]));
  Multiplexer #(.enable("false")) multiplexer_101 (
    .in0(multiplexer_70_out), .in1(multiplexer_78_out), .out(multiplexer_101_out), .sel(Move[3]));
  Multiplexer #(.enable("false")) multiplexer_102 (
    .in0(multiplexer_71_out), .in1(multiplexer_79_out), .out(multiplexer_102_out), .sel(Move[3]));
  Multiplexer #(.enable("false")) multiplexer_103 (
    .in0(multiplexer_72_out), .in1(multiplexer_80_out), .out(multiplexer_103_out), .sel(Move[3]));
  Multiplexer #(.enable("false")) multiplexer_104 (
    .in0(multiplexer_73_out), .in1(multiplexer_81_out), .out(multiplexer_104_out), .sel(Move[3]));
  Multiplexer #(.enable("false")) multiplexer_105 (
    .in0(multiplexer_74_out), .in1(multiplexer_82_out), .out(multiplexer_105_out), .sel(Move[3]));
  Multiplexer #(.enable("false")) multiplexer_106 (
    .in0(multiplexer_75_out), .in1(multiplexer_83_out), .out(multiplexer_106_out), .sel(Move[3]));
  Multiplexer #(.enable("false")) multiplexer_107 (
    .in0(multiplexer_76_out), .in1(multiplexer_84_out), .out(multiplexer_107_out), .sel(Move[3]));
  Multiplexer #(.enable("false")) multiplexer_108 (
    .in0(multiplexer_77_out), .in1(multiplexer_85_out), .out(multiplexer_108_out), .sel(Move[3]));
  Multiplexer #(.enable("false")) multiplexer_109 (
    .in0(multiplexer_78_out), .in1(multiplexer_86_out), .out(multiplexer_109_out), .sel(Move[3]));
  Multiplexer #(.enable("false")) multiplexer_110 (
    .in0(multiplexer_79_out), .in1(multiplexer_87_out), .out(multiplexer_110_out), .sel(Move[3]));
  Multiplexer #(.enable("false")) multiplexer_111 (
    .in0(multiplexer_80_out), .in1(multiplexer_88_out), .out(multiplexer_111_out), .sel(Move[3]));
  Multiplexer #(.enable("false")) multiplexer_112 (
    .in0(multiplexer_81_out), .in1(multiplexer_89_out), .out(multiplexer_112_out), .sel(Move[3]));
  Multiplexer #(.enable("false")) multiplexer_113 (
    .in0(multiplexer_82_out), .in1(multiplexer_90_out), .out(multiplexer_113_out), .sel(Move[3]));
  Multiplexer #(.enable("false")) multiplexer_114 (
    .in0(multiplexer_83_out), .in1(multiplexer_91_out), .out(multiplexer_114_out), .sel(Move[3]));
  Multiplexer #(.enable("false")) multiplexer_115 (
    .in0(multiplexer_84_out), .in1(multiplexer_92_out), .out(multiplexer_115_out), .sel(Move[3]));
  Multiplexer #(.enable("false")) multiplexer_116 (
    .in0(multiplexer_85_out), .in1(multiplexer_93_out), .out(multiplexer_116_out), .sel(Move[3]));
  Multiplexer #(.enable("false")) multiplexer_117 (
    .in0(multiplexer_86_out), .in1(A[31]), .out(multiplexer_117_out), .sel(Move[3]));
  Multiplexer #(.enable("false")) multiplexer_118 (
    .in0(multiplexer_87_out), .in1(A[31]), .out(multiplexer_118_out), .sel(Move[3]));
  Multiplexer #(.enable("false")) multiplexer_119 (
    .in0(multiplexer_88_out), .in1(A[31]), .out(multiplexer_119_out), .sel(Move[3]));
  Multiplexer #(.enable("false")) multiplexer_120 (
    .in0(multiplexer_89_out), .in1(A[31]), .out(multiplexer_120_out), .sel(Move[3]));
  Multiplexer #(.enable("false")) multiplexer_121 (
    .in0(multiplexer_90_out), .in1(A[31]), .out(multiplexer_121_out), .sel(Move[3]));
  Multiplexer #(.enable("false")) multiplexer_122 (
    .in0(multiplexer_91_out), .in1(A[31]), .out(multiplexer_122_out), .sel(Move[3]));
  Multiplexer #(.enable("false")) multiplexer_123 (
    .in0(multiplexer_92_out), .in1(A[31]), .out(multiplexer_123_out), .sel(Move[3]));
  Multiplexer #(.enable("false")) multiplexer_124 (
    .in0(multiplexer_93_out), .in1(A[31]), .out(multiplexer_124_out), .sel(Move[3]));
  Multiplexer #(.enable("false")) multiplexer_125 (
    .in0(multiplexer_94_out), .in1(multiplexer_110_out), .out(S[0]), .sel(Move[4]));
  Multiplexer #(.enable("false")) multiplexer_126 (
    .in0(multiplexer_95_out), .in1(multiplexer_111_out), .out(S[1]), .sel(Move[4]));
  Multiplexer #(.enable("false")) multiplexer_127 (
    .in0(multiplexer_96_out), .in1(multiplexer_112_out), .out(S[2]), .sel(Move[4]));
  Multiplexer #(.enable("false")) multiplexer_128 (
    .in0(multiplexer_97_out), .in1(multiplexer_113_out), .out(S[3]), .sel(Move[4]));
  Multiplexer #(.enable("false")) multiplexer_129 (
    .in0(multiplexer_98_out), .in1(multiplexer_114_out), .out(S[4]), .sel(Move[4]));
  Multiplexer #(.enable("false")) multiplexer_130 (
    .in0(multiplexer_99_out), .in1(multiplexer_115_out), .out(S[5]), .sel(Move[4]));
  Multiplexer #(.enable("false")) multiplexer_131 (
    .in0(multiplexer_100_out), .in1(multiplexer_116_out), .out(S[6]), .sel(Move[4]));
  Multiplexer #(.enable("false")) multiplexer_132 (
    .in0(multiplexer_101_out), .in1(multiplexer_117_out), .out(S[7]), .sel(Move[4]));
  Multiplexer #(.enable("false")) multiplexer_133 (
    .in0(multiplexer_102_out), .in1(multiplexer_118_out), .out(S[8]), .sel(Move[4]));
  Multiplexer #(.enable("false")) multiplexer_134 (
    .in0(multiplexer_103_out), .in1(multiplexer_119_out), .out(S[9]), .sel(Move[4]));
  Multiplexer #(.enable("false")) multiplexer_135 (
    .in0(multiplexer_104_out), .in1(multiplexer_120_out), .out(S[10]), .sel(Move[4]));
  Multiplexer #(.enable("false")) multiplexer_136 (
    .in0(multiplexer_105_out), .in1(multiplexer_121_out), .out(S[11]), .sel(Move[4]));
  Multiplexer #(.enable("false")) multiplexer_137 (
    .in0(multiplexer_106_out), .in1(multiplexer_122_out), .out(S[12]), .sel(Move[4]));
  Multiplexer #(.enable("false")) multiplexer_138 (
    .in0(multiplexer_107_out), .in1(multiplexer_123_out), .out(S[13]), .sel(Move[4]));
  Multiplexer #(.enable("false")) multiplexer_139 (
    .in0(multiplexer_108_out), .in1(multiplexer_124_out), .out(S[14]), .sel(Move[4]));
  Multiplexer #(.enable("false")) multiplexer_140 (.in0(multiplexer_109_out), .in1(A[31]), .out(S[15]), .sel(Move[4]));
  Multiplexer #(.enable("false")) multiplexer_141 (.in0(multiplexer_110_out), .in1(A[31]), .out(S[16]), .sel(Move[4]));
  Multiplexer #(.enable("false")) multiplexer_142 (.in0(multiplexer_111_out), .in1(A[31]), .out(S[17]), .sel(Move[4]));
  Multiplexer #(.enable("false")) multiplexer_143 (.in0(multiplexer_112_out), .in1(A[31]), .out(S[18]), .sel(Move[4]));
  Multiplexer #(.enable("false")) multiplexer_144 (.in0(multiplexer_113_out), .in1(A[31]), .out(S[19]), .sel(Move[4]));
  Multiplexer #(.enable("false")) multiplexer_145 (.in0(multiplexer_114_out), .in1(A[31]), .out(S[20]), .sel(Move[4]));
  Multiplexer #(.enable("false")) multiplexer_146 (.in0(multiplexer_115_out), .in1(A[31]), .out(S[21]), .sel(Move[4]));
  Multiplexer #(.enable("false")) multiplexer_147 (.in0(multiplexer_116_out), .in1(A[31]), .out(S[22]), .sel(Move[4]));
  Multiplexer #(.enable("false")) multiplexer_148 (.in0(multiplexer_117_out), .in1(A[31]), .out(S[23]), .sel(Move[4]));
  Multiplexer #(.enable("false")) multiplexer_149 (.in0(multiplexer_118_out), .in1(A[31]), .out(S[24]), .sel(Move[4]));
  Multiplexer #(.enable("false")) multiplexer_150 (.in0(multiplexer_119_out), .in1(A[31]), .out(S[25]), .sel(Move[4]));
  Multiplexer #(.enable("false")) multiplexer_151 (.in0(multiplexer_120_out), .in1(A[31]), .out(S[26]), .sel(Move[4]));
  Multiplexer #(.enable("false")) multiplexer_152 (.in0(multiplexer_121_out), .in1(A[31]), .out(S[27]), .sel(Move[4]));
  Multiplexer #(.enable("false")) multiplexer_153 (.in0(multiplexer_122_out), .in1(A[31]), .out(S[28]), .sel(Move[4]));
  Multiplexer #(.enable("false")) multiplexer_154 (.in0(multiplexer_123_out), .in1(A[31]), .out(S[29]), .sel(Move[4]));
  Multiplexer #(.enable("false")) multiplexer_155 (.in0(multiplexer_124_out), .in1(A[31]), .out(S[30]), .sel(Move[4]));

  assign S[31] = A[31];
endmodule

module ula (
  input  [31:0] A,
  input  [4:0] OpeCode,
  input  [4:0] move,
  input  [31:0] B,
  output zero,
  output OverFlow,
  output [31:0] S
);

  wire and_1_out, and_2_out, and_3_out, and_4_out, multiplexer_1_out, not_1_out, or_1_out, ula_cel_1_cout,
       ula_cel_2_cout, ula_cel_3_cout, ula_cel_4_cout, ula_cel_5_cout, ula_cel_6_cout, ula_cel_7_cout,
       ula_cel_8_cout, ula_cel_9_cout, ula_cel_10_cout, ula_cel_11_cout, ula_cel_12_cout, ula_cel_13_cout,
       ula_cel_14_cout, ula_cel_15_cout, ula_cel_16_cout, ula_cel_17_cout, ula_cel_18_cout, ula_cel_19_cout,
       ula_cel_20_cout, ula_cel_21_cout, ula_cel_22_cout, ula_cel_23_cout, ula_cel_24_cout, ula_cel_25_cout,
       ula_cel_26_cout, ula_cel_27_cout, ula_cel_28_cout, ula_cel_29_cout, ula_cel_30_cout, ula_cel_31_cout,
       ula_cel_32_cout;
  wire [7:0] deslocador_1_s, deslocador_1_s_2, deslocador_1_s_3, deslocador_1_s_4, ula_cel_1_s, ula_cel_2_s,
       ula_cel_3_s, ula_cel_4_s;

  and and_1 (and_1_out, OpeCode[0], ~OpeCode[1], OpeCode[2], OpeCode[3], OpeCode[4]);  // AND_Gate
  or or_1 (or_1_out, and_1_out, and_2_out, and_3_out, and_4_out);
  and and_2 (and_2_out, ~OpeCode[0], OpeCode[1], OpeCode[2], OpeCode[3], OpeCode[4]);  // AND_Gate
  and and_3 (and_3_out, ~OpeCode[4], OpeCode[3], ~OpeCode[2], OpeCode[1], OpeCode[0]);  // AND_Gate
  and and_4 (and_4_out, ~OpeCode[4], ~OpeCode[3], OpeCode[2], OpeCode[1], ~OpeCode[0]);  // AND_Gate
  not not_1 (not_1_out, 1'b0);
  Multiplexer #(.enable("false")) multiplexer_1 (.in0(1'b0), .in1(not_1_out), .out(multiplexer_1_out), .sel(or_1_out));
  ula_cel ula_cel_1 (
    .Cin(multiplexer_1_out), .a(deslocador_1_s[0]), .b(B[0]), .Select(OpeCode), .S(ula_cel_1_s[0]),
    .Cout(ula_cel_1_cout));
  ula_cel ula_cel_2 (
    .Cin(ula_cel_29_cout), .a(deslocador_1_s_2[0]), .b(B[8]), .Select(OpeCode), .S(ula_cel_2_s[0]),
    .Cout(ula_cel_2_cout));
  ula_cel ula_cel_3 (
    .Cin(ula_cel_30_cout), .a(deslocador_1_s_3[0]), .b(B[16]), .Select(OpeCode), .S(ula_cel_3_s[0]),
    .Cout(ula_cel_3_cout));
  ula_cel ula_cel_4 (
    .Cin(ula_cel_31_cout), .a(deslocador_1_s_4[0]), .b(B[24]), .Select(OpeCode), .S(ula_cel_4_s[0]),
    .Cout(ula_cel_4_cout));
  ula_cel ula_cel_5 (
    .Cin(ula_cel_1_cout), .a(deslocador_1_s[1]), .b(B[1]), .Select(OpeCode), .S(ula_cel_1_s[1]),
    .Cout(ula_cel_5_cout));
  ula_cel ula_cel_6 (
    .Cin(ula_cel_2_cout), .a(deslocador_1_s_2[1]), .b(B[9]), .Select(OpeCode), .S(ula_cel_2_s[1]),
    .Cout(ula_cel_6_cout));
  ula_cel ula_cel_7 (
    .Cin(ula_cel_3_cout), .a(deslocador_1_s_3[1]), .b(B[17]), .Select(OpeCode), .S(ula_cel_3_s[1]),
    .Cout(ula_cel_7_cout));
  ula_cel ula_cel_8 (
    .Cin(ula_cel_4_cout), .a(deslocador_1_s_4[1]), .b(B[25]), .Select(OpeCode), .S(ula_cel_4_s[1]),
    .Cout(ula_cel_8_cout));
  ula_cel ula_cel_9 (
    .Cin(ula_cel_5_cout), .a(deslocador_1_s[2]), .b(B[2]), .Select(OpeCode), .S(ula_cel_1_s[2]),
    .Cout(ula_cel_9_cout));
  ula_cel ula_cel_10 (
    .Cin(ula_cel_6_cout), .a(deslocador_1_s_2[2]), .b(B[10]), .Select(OpeCode), .S(ula_cel_2_s[2]),
    .Cout(ula_cel_10_cout));
  ula_cel ula_cel_11 (
    .Cin(ula_cel_7_cout), .a(deslocador_1_s_3[2]), .b(B[18]), .Select(OpeCode), .S(ula_cel_3_s[2]),
    .Cout(ula_cel_11_cout));
  ula_cel ula_cel_12 (
    .Cin(ula_cel_8_cout), .a(deslocador_1_s_4[2]), .b(B[26]), .Select(OpeCode), .S(ula_cel_4_s[2]),
    .Cout(ula_cel_12_cout));
  ula_cel ula_cel_13 (
    .Cin(ula_cel_9_cout), .a(deslocador_1_s[3]), .b(B[3]), .Select(OpeCode), .S(ula_cel_1_s[3]),
    .Cout(ula_cel_13_cout));
  ula_cel ula_cel_14 (
    .Cin(ula_cel_10_cout), .a(deslocador_1_s_2[3]), .b(B[11]), .Select(OpeCode), .S(ula_cel_2_s[3]),
    .Cout(ula_cel_14_cout));
  ula_cel ula_cel_15 (
    .Cin(ula_cel_11_cout), .a(deslocador_1_s_3[3]), .b(B[19]), .Select(OpeCode), .S(ula_cel_3_s[3]),
    .Cout(ula_cel_15_cout));
  ula_cel ula_cel_16 (
    .Cin(ula_cel_12_cout), .a(deslocador_1_s_4[3]), .b(B[27]), .Select(OpeCode), .S(ula_cel_4_s[3]),
    .Cout(ula_cel_16_cout));
  ula_cel ula_cel_17 (
    .Cin(ula_cel_13_cout), .a(deslocador_1_s[4]), .b(B[4]), .Select(OpeCode), .S(ula_cel_1_s[4]),
    .Cout(ula_cel_17_cout));
  ula_cel ula_cel_18 (
    .Cin(ula_cel_14_cout), .a(deslocador_1_s_2[4]), .b(B[12]), .Select(OpeCode), .S(ula_cel_2_s[4]),
    .Cout(ula_cel_18_cout));
  ula_cel ula_cel_19 (
    .Cin(ula_cel_15_cout), .a(deslocador_1_s_3[4]), .b(B[20]), .Select(OpeCode), .S(ula_cel_3_s[4]),
    .Cout(ula_cel_19_cout));
  ula_cel ula_cel_20 (
    .Cin(ula_cel_16_cout), .a(deslocador_1_s_4[4]), .b(B[28]), .Select(OpeCode), .S(ula_cel_4_s[4]),
    .Cout(ula_cel_20_cout));
  ula_cel ula_cel_21 (
    .Cin(ula_cel_17_cout), .a(deslocador_1_s[5]), .b(B[5]), .Select(OpeCode), .S(ula_cel_1_s[5]),
    .Cout(ula_cel_21_cout));
  ula_cel ula_cel_22 (
    .Cin(ula_cel_18_cout), .a(deslocador_1_s_2[5]), .b(B[13]), .Select(OpeCode), .S(ula_cel_2_s[5]),
    .Cout(ula_cel_22_cout));
  ula_cel ula_cel_23 (
    .Cin(ula_cel_19_cout), .a(deslocador_1_s_3[5]), .b(B[21]), .Select(OpeCode), .S(ula_cel_3_s[5]),
    .Cout(ula_cel_23_cout));
  ula_cel ula_cel_24 (
    .Cin(ula_cel_20_cout), .a(deslocador_1_s_4[5]), .b(B[29]), .Select(OpeCode), .S(ula_cel_4_s[5]),
    .Cout(ula_cel_24_cout));
  ula_cel ula_cel_25 (
    .Cin(ula_cel_21_cout), .a(deslocador_1_s[6]), .b(B[6]), .Select(OpeCode), .S(ula_cel_1_s[6]),
    .Cout(ula_cel_25_cout));
  ula_cel ula_cel_26 (
    .Cin(ula_cel_22_cout), .a(deslocador_1_s_2[6]), .b(B[14]), .Select(OpeCode), .S(ula_cel_2_s[6]),
    .Cout(ula_cel_26_cout));
  ula_cel ula_cel_27 (
    .Cin(ula_cel_23_cout), .a(deslocador_1_s_3[6]), .b(B[22]), .Select(OpeCode), .S(ula_cel_3_s[6]),
    .Cout(ula_cel_27_cout));
  ula_cel ula_cel_28 (
    .Cin(ula_cel_24_cout), .a(deslocador_1_s_4[6]), .b(B[30]), .Select(OpeCode), .S(ula_cel_4_s[6]),
    .Cout(ula_cel_28_cout));
  ula_cel ula_cel_29 (
    .Cin(ula_cel_25_cout), .a(deslocador_1_s[7]), .b(B[7]), .Select(OpeCode), .S(ula_cel_1_s[7]),
    .Cout(ula_cel_29_cout));
  ula_cel ula_cel_30 (
    .Cin(ula_cel_26_cout), .a(deslocador_1_s_2[7]), .b(B[15]), .Select(OpeCode), .S(ula_cel_2_s[7]),
    .Cout(ula_cel_30_cout));
  ula_cel ula_cel_31 (
    .Cin(ula_cel_27_cout), .a(deslocador_1_s_3[7]), .b(B[23]), .Select(OpeCode), .S(ula_cel_3_s[7]),
    .Cout(ula_cel_31_cout));
  ula_cel ula_cel_32 (
    .Cin(ula_cel_28_cout), .a(deslocador_1_s_4[7]), .b(B[31]), .Select(OpeCode), .S(ula_cel_4_s[7]),
    .Cout(ula_cel_32_cout));
  overflow overflow_1 (
    .OpeCode(OpeCode), .Cin(ula_cel_32_cout), .S(ula_cel_4_s[7]), .b(B[31]), .a(deslocador_1_s_4[7]),
    .OverFlow(OverFlow));
  deslocador deslocador_1 (
    .A(A), .move(move), .OpeCode(OpeCode),
    .S({deslocador_1_s_4, deslocador_1_s_3, deslocador_1_s_2, deslocador_1_s}));
  SLT slt_1 (.OpeCode(OpeCode), .Sin({ula_cel_4_s, ula_cel_3_s, ula_cel_2_s, ula_cel_1_s}), .Sout(S));
  nor nor_1 (zero, ula_cel_1_s[0], ula_cel_1_s[1], ula_cel_1_s[2], ula_cel_1_s[3], ula_cel_1_s[4], ula_cel_1_s[5], ula_cel_1_s[6], ula_cel_1_s[7], ula_cel_2_s[0], ula_cel_2_s[1], ula_cel_2_s[2], ula_cel_2_s[3], ula_cel_2_s[4], ula_cel_2_s[5], ula_cel_2_s[6], ula_cel_2_s[7], ula_cel_3_s[0], ula_cel_3_s[1], ula_cel_3_s[2], ula_cel_3_s[3], ula_cel_3_s[4], ula_cel_3_s[5], ula_cel_3_s[6], ula_cel_3_s[7], ula_cel_4_s[0], ula_cel_4_s[1], ula_cel_4_s[2], ula_cel_4_s[3], ula_cel_4_s[4], ula_cel_4_s[5], ula_cel_4_s[6], ula_cel_4_s[7]);

  // Notes on the sheet:
  //   01011 - SLT
  //   01100 - Soma Constante
  //   00000 - And
  //   00001 - Or
  //   00010 - XOR
  //   00011 - NAND
  //   00100 - Soma naturais
  //   00101 - Soma inteiros
  //   00110 - Subtração
  //   00111 - Deslocamento Esquerda
  //   01000 - Deslocamento Direita
  //   01001 - Deslocamento Direita Aritimética
  //   01010 - ROL
endmodule

module registrador (
  input  [31:0] Data,
  input  wr,
  output [31:0] s
);

  D_Flip_Flop d_ff_1 (.clk(wr), .D(Data[31]), .Q(s[31]));  // open: Qn, preset, en, reset
  D_Flip_Flop d_ff_2 (.clk(wr), .D(Data[30]), .Q(s[30]));  // open: Qn, preset, en, reset
  D_Flip_Flop d_ff_3 (.clk(wr), .D(Data[29]), .Q(s[29]));  // open: Qn, preset, en, reset
  D_Flip_Flop d_ff_4 (.clk(wr), .D(Data[28]), .Q(s[28]));  // open: Qn, preset, en, reset
  D_Flip_Flop d_ff_5 (.clk(wr), .D(Data[27]), .Q(s[27]));  // open: Qn, preset, en, reset
  D_Flip_Flop d_ff_6 (.clk(wr), .D(Data[26]), .Q(s[26]));  // open: Qn, preset, en, reset
  D_Flip_Flop d_ff_7 (.clk(wr), .D(Data[25]), .Q(s[25]));  // open: Qn, preset, en, reset
  D_Flip_Flop d_ff_8 (.clk(wr), .D(Data[24]), .Q(s[24]));  // open: Qn, preset, en, reset
  D_Flip_Flop d_ff_9 (.clk(wr), .D(Data[23]), .Q(s[23]));  // open: Qn, preset, en, reset
  D_Flip_Flop d_ff_10 (.clk(wr), .D(Data[22]), .Q(s[22]));  // open: Qn, preset, en, reset
  D_Flip_Flop d_ff_11 (.clk(wr), .D(Data[21]), .Q(s[21]));  // open: Qn, preset, en, reset
  D_Flip_Flop d_ff_12 (.clk(wr), .D(Data[20]), .Q(s[20]));  // open: Qn, preset, en, reset
  D_Flip_Flop d_ff_13 (.clk(wr), .D(Data[19]), .Q(s[19]));  // open: Qn, preset, en, reset
  D_Flip_Flop d_ff_14 (.clk(wr), .D(Data[18]), .Q(s[18]));  // open: Qn, preset, en, reset
  D_Flip_Flop d_ff_15 (.clk(wr), .D(Data[17]), .Q(s[17]));  // open: Qn, preset, en, reset
  D_Flip_Flop d_ff_16 (.clk(wr), .D(Data[16]), .Q(s[16]));  // open: Qn, preset, en, reset
  D_Flip_Flop d_ff_17 (.clk(wr), .D(Data[15]), .Q(s[15]));  // open: Qn, preset, en, reset
  D_Flip_Flop d_ff_18 (.clk(wr), .D(Data[14]), .Q(s[14]));  // open: Qn, preset, en, reset
  D_Flip_Flop d_ff_19 (.clk(wr), .D(Data[13]), .Q(s[13]));  // open: Qn, preset, en, reset
  D_Flip_Flop d_ff_20 (.clk(wr), .D(Data[12]), .Q(s[12]));  // open: Qn, preset, en, reset
  D_Flip_Flop d_ff_21 (.clk(wr), .D(Data[11]), .Q(s[11]));  // open: Qn, preset, en, reset
  D_Flip_Flop d_ff_22 (.clk(wr), .D(Data[10]), .Q(s[10]));  // open: Qn, preset, en, reset
  D_Flip_Flop d_ff_23 (.clk(wr), .D(Data[9]), .Q(s[9]));  // open: Qn, preset, en, reset
  D_Flip_Flop d_ff_24 (.clk(wr), .D(Data[8]), .Q(s[8]));  // open: Qn, preset, en, reset
  D_Flip_Flop d_ff_25 (.clk(wr), .D(Data[7]), .Q(s[7]));  // open: Qn, preset, en, reset
  D_Flip_Flop d_ff_26 (.clk(wr), .D(Data[6]), .Q(s[6]));  // open: Qn, preset, en, reset
  D_Flip_Flop d_ff_27 (.clk(wr), .D(Data[5]), .Q(s[5]));  // open: Qn, preset, en, reset
  D_Flip_Flop d_ff_28 (.clk(wr), .D(Data[4]), .Q(s[4]));  // open: Qn, preset, en, reset
  D_Flip_Flop d_ff_29 (.clk(wr), .D(Data[3]), .Q(s[3]));  // open: Qn, preset, en, reset
  D_Flip_Flop d_ff_30 (.clk(wr), .D(Data[2]), .Q(s[2]));  // open: Qn, preset, en, reset
  D_Flip_Flop d_ff_31 (.clk(wr), .D(Data[1]), .Q(s[1]));  // open: Qn, preset, en, reset
  D_Flip_Flop d_ff_32 (.clk(wr), .D(Data[0]), .Q(s[0]));  // open: Qn, preset, en, reset
endmodule
module bancoDeRes (
  input  [4:0] seletorRegistrador,
  input  wr,
  input  [31:0] a,
  input  [4:0] seletor_registrador_B,
  input  [4:0] seletor_registrador_A,
  output [31:0] A_2,
  output [31:0] B
);

  wire demultiplexer_1_out0, demultiplexer_1_out1, demultiplexer_1_out2, demultiplexer_1_out3,
       demultiplexer_1_out4, demultiplexer_1_out5, demultiplexer_1_out6, demultiplexer_1_out7,
       demultiplexer_1_out8, demultiplexer_1_out9, demultiplexer_1_out10, demultiplexer_1_out11,
       demultiplexer_1_out12, demultiplexer_1_out13, demultiplexer_1_out14, demultiplexer_1_out15,
       demultiplexer_1_out16, demultiplexer_1_out17, demultiplexer_1_out18, demultiplexer_1_out19,
       demultiplexer_1_out20, demultiplexer_1_out21, demultiplexer_1_out22, demultiplexer_1_out23,
       demultiplexer_1_out24, demultiplexer_1_out25, demultiplexer_1_out26, demultiplexer_1_out27,
       demultiplexer_1_out28, demultiplexer_1_out29, demultiplexer_1_out30, demultiplexer_1_out31;
  wire [31:0] registrador_1_s, registrador_2_s, registrador_3_s, registrador_4_s, registrador_5_s,
       registrador_6_s, registrador_7_s, registrador_8_s, registrador_9_s, registrador_10_s,
       registrador_11_s, registrador_12_s, registrador_13_s, registrador_14_s, registrador_15_s,
       registrador_16_s, registrador_17_s, registrador_18_s, registrador_19_s, registrador_20_s,
       registrador_21_s, registrador_22_s, registrador_23_s, registrador_24_s, registrador_25_s,
       registrador_26_s, registrador_27_s, registrador_28_s, registrador_29_s, registrador_30_s,
       registrador_31_s, registrador_32_s;

  registrador registrador_1 (.Data({32{1'b0}}), .wr(demultiplexer_1_out0), .s(registrador_1_s));
  registrador registrador_2 (.Data(a), .wr(demultiplexer_1_out1), .s(registrador_2_s));
  registrador registrador_3 (.Data(a), .wr(demultiplexer_1_out2), .s(registrador_3_s));
  registrador registrador_4 (.Data(a), .wr(demultiplexer_1_out3), .s(registrador_4_s));
  registrador registrador_5 (.Data(a), .wr(demultiplexer_1_out4), .s(registrador_5_s));
  registrador registrador_6 (.Data(a), .wr(demultiplexer_1_out5), .s(registrador_6_s));
  registrador registrador_7 (.Data(a), .wr(demultiplexer_1_out6), .s(registrador_7_s));
  registrador registrador_8 (.Data(a), .wr(demultiplexer_1_out7), .s(registrador_8_s));
  registrador registrador_9 (.Data(a), .wr(demultiplexer_1_out8), .s(registrador_9_s));
  registrador registrador_10 (.Data(a), .wr(demultiplexer_1_out9), .s(registrador_10_s));
  registrador registrador_11 (.Data(a), .wr(demultiplexer_1_out10), .s(registrador_11_s));
  registrador registrador_12 (.Data(a), .wr(demultiplexer_1_out11), .s(registrador_12_s));
  registrador registrador_13 (.Data(a), .wr(demultiplexer_1_out12), .s(registrador_13_s));
  registrador registrador_14 (.Data(a), .wr(demultiplexer_1_out13), .s(registrador_14_s));
  registrador registrador_15 (.Data(a), .wr(demultiplexer_1_out14), .s(registrador_15_s));
  registrador registrador_16 (.Data(a), .wr(demultiplexer_1_out15), .s(registrador_16_s));
  registrador registrador_17 (.Data(a), .wr(demultiplexer_1_out16), .s(registrador_17_s));
  registrador registrador_18 (.Data(a), .wr(demultiplexer_1_out17), .s(registrador_18_s));
  registrador registrador_19 (.Data(a), .wr(demultiplexer_1_out18), .s(registrador_19_s));
  registrador registrador_20 (.Data(a), .wr(demultiplexer_1_out19), .s(registrador_20_s));
  registrador registrador_21 (.Data(a), .wr(demultiplexer_1_out20), .s(registrador_21_s));
  registrador registrador_22 (.Data(a), .wr(demultiplexer_1_out21), .s(registrador_22_s));
  registrador registrador_23 (.Data(a), .wr(demultiplexer_1_out22), .s(registrador_23_s));
  registrador registrador_24 (.Data(a), .wr(demultiplexer_1_out23), .s(registrador_24_s));
  registrador registrador_25 (.Data(a), .wr(demultiplexer_1_out24), .s(registrador_25_s));
  registrador registrador_26 (.Data(a), .wr(demultiplexer_1_out25), .s(registrador_26_s));
  registrador registrador_27 (.Data(a), .wr(demultiplexer_1_out26), .s(registrador_27_s));
  registrador registrador_28 (.Data(a), .wr(demultiplexer_1_out27), .s(registrador_28_s));
  registrador registrador_29 (.Data(a), .wr(demultiplexer_1_out28), .s(registrador_29_s));
  registrador registrador_30 (.Data(a), .wr(demultiplexer_1_out29), .s(registrador_30_s));
  registrador registrador_31 (.Data(a), .wr(demultiplexer_1_out30), .s(registrador_31_s));
  registrador registrador_32 (.Data(a), .wr(demultiplexer_1_out31), .s(registrador_32_s));
  Demultiplexer #(.select(5), .enable("false")) demultiplexer_1 (
    .out0(demultiplexer_1_out0), .out1(demultiplexer_1_out1), .out2(demultiplexer_1_out2),
    .out3(demultiplexer_1_out3), .out4(demultiplexer_1_out4), .out5(demultiplexer_1_out5),
    .out6(demultiplexer_1_out6), .out7(demultiplexer_1_out7), .out8(demultiplexer_1_out8),
    .out9(demultiplexer_1_out9), .out10(demultiplexer_1_out10), .out11(demultiplexer_1_out11),
    .out12(demultiplexer_1_out12), .out13(demultiplexer_1_out13), .out14(demultiplexer_1_out14),
    .out15(demultiplexer_1_out15), .out16(demultiplexer_1_out16), .out17(demultiplexer_1_out17),
    .out18(demultiplexer_1_out18), .out19(demultiplexer_1_out19), .out20(demultiplexer_1_out20),
    .out21(demultiplexer_1_out21), .out22(demultiplexer_1_out22), .out23(demultiplexer_1_out23),
    .out24(demultiplexer_1_out24), .out25(demultiplexer_1_out25), .out26(demultiplexer_1_out26),
    .out27(demultiplexer_1_out27), .out28(demultiplexer_1_out28), .out29(demultiplexer_1_out29),
    .out30(demultiplexer_1_out30), .out31(demultiplexer_1_out31), .in(wr), .sel(seletorRegistrador));
  Multiplexer #(.select(5), .width(32), .enable("false")) multiplexer_1 (
    .in0(registrador_1_s), .in1(registrador_2_s), .in2(registrador_3_s), .in3(registrador_4_s),
    .in4(registrador_5_s), .in5(registrador_6_s), .in6(registrador_7_s), .in7(registrador_8_s),
    .in8(registrador_9_s), .in9(registrador_10_s), .in10(registrador_11_s), .in11(registrador_12_s),
    .in12(registrador_13_s), .in13(registrador_14_s), .in14(registrador_15_s), .in15(registrador_16_s),
    .in16(registrador_17_s), .in17(registrador_18_s), .in18(registrador_19_s), .in19(registrador_20_s),
    .in20(registrador_21_s), .in21(registrador_22_s), .in22(registrador_23_s), .in23(registrador_24_s),
    .in24(registrador_25_s), .in25(registrador_26_s), .in26(registrador_27_s), .in27(registrador_28_s),
    .in28(registrador_29_s), .in29(registrador_30_s), .in30(registrador_31_s), .in31(registrador_32_s),
    .out(B), .sel(seletor_registrador_B));
  Multiplexer #(.select(5), .width(32), .enable("false")) multiplexer_2 (
    .in0(registrador_1_s), .in1(registrador_2_s), .in2(registrador_3_s), .in3(registrador_4_s),
    .in4(registrador_5_s), .in5(registrador_6_s), .in6(registrador_7_s), .in7(registrador_8_s),
    .in8(registrador_9_s), .in9(registrador_10_s), .in10(registrador_11_s), .in11(registrador_12_s),
    .in12(registrador_13_s), .in13(registrador_14_s), .in14(registrador_15_s), .in15(registrador_16_s),
    .in16(registrador_17_s), .in17(registrador_18_s), .in18(registrador_19_s), .in19(registrador_20_s),
    .in20(registrador_21_s), .in21(registrador_22_s), .in22(registrador_23_s), .in23(registrador_24_s),
    .in24(registrador_25_s), .in25(registrador_26_s), .in26(registrador_27_s), .in27(registrador_28_s),
    .in28(registrador_29_s), .in29(registrador_30_s), .in30(registrador_31_s), .in31(registrador_32_s),
    .out(A_2), .sel(seletor_registrador_A));
endmodule

module rol (
  input  [31:0] A,
  input  [4:0] Move,
  output [31:0] S
);

  wire multiplexer_1_out, multiplexer_2_out, multiplexer_3_out, multiplexer_4_out, multiplexer_5_out,
       multiplexer_6_out, multiplexer_7_out, multiplexer_8_out, multiplexer_9_out, multiplexer_10_out,
       multiplexer_11_out, multiplexer_12_out, multiplexer_13_out, multiplexer_14_out, multiplexer_15_out,
       multiplexer_16_out, multiplexer_17_out, multiplexer_18_out, multiplexer_19_out, multiplexer_20_out,
       multiplexer_21_out, multiplexer_22_out, multiplexer_23_out, multiplexer_24_out, multiplexer_25_out,
       multiplexer_26_out, multiplexer_27_out, multiplexer_28_out, multiplexer_29_out, multiplexer_30_out,
       multiplexer_31_out, multiplexer_32_out, multiplexer_33_out, multiplexer_34_out, multiplexer_35_out,
       multiplexer_36_out, multiplexer_37_out, multiplexer_38_out, multiplexer_39_out, multiplexer_40_out,
       multiplexer_41_out, multiplexer_42_out, multiplexer_43_out, multiplexer_44_out, multiplexer_45_out,
       multiplexer_46_out, multiplexer_47_out, multiplexer_48_out, multiplexer_49_out, multiplexer_50_out,
       multiplexer_51_out, multiplexer_52_out, multiplexer_53_out, multiplexer_54_out, multiplexer_55_out,
       multiplexer_56_out, multiplexer_57_out, multiplexer_58_out, multiplexer_59_out, multiplexer_60_out,
       multiplexer_61_out, multiplexer_62_out, multiplexer_63_out, multiplexer_64_out, multiplexer_65_out,
       multiplexer_66_out, multiplexer_67_out, multiplexer_68_out, multiplexer_69_out, multiplexer_70_out,
       multiplexer_71_out, multiplexer_72_out, multiplexer_73_out, multiplexer_74_out, multiplexer_75_out,
       multiplexer_76_out, multiplexer_77_out, multiplexer_78_out, multiplexer_79_out, multiplexer_80_out,
       multiplexer_81_out, multiplexer_82_out, multiplexer_83_out, multiplexer_84_out, multiplexer_85_out,
       multiplexer_86_out, multiplexer_87_out, multiplexer_88_out, multiplexer_89_out, multiplexer_90_out,
       multiplexer_91_out, multiplexer_92_out, multiplexer_93_out, multiplexer_94_out, multiplexer_95_out,
       multiplexer_96_out, multiplexer_97_out, multiplexer_98_out, multiplexer_99_out, multiplexer_100_out,
       multiplexer_101_out, multiplexer_102_out, multiplexer_103_out, multiplexer_104_out,
       multiplexer_105_out, multiplexer_106_out, multiplexer_107_out, multiplexer_108_out,
       multiplexer_109_out, multiplexer_110_out, multiplexer_111_out, multiplexer_112_out,
       multiplexer_113_out, multiplexer_114_out, multiplexer_115_out, multiplexer_116_out,
       multiplexer_117_out, multiplexer_118_out, multiplexer_119_out, multiplexer_120_out,
       multiplexer_121_out, multiplexer_122_out, multiplexer_123_out, multiplexer_124_out,
       multiplexer_125_out, multiplexer_126_out, multiplexer_127_out, multiplexer_128_out;

  Multiplexer #(.enable("false")) multiplexer_1 (.in0(A[31]), .in1(A[30]), .out(multiplexer_1_out), .sel(Move[0]));
  Multiplexer #(.enable("false")) multiplexer_2 (.in0(A[30]), .in1(A[29]), .out(multiplexer_2_out), .sel(Move[0]));
  Multiplexer #(.enable("false")) multiplexer_3 (.in0(A[29]), .in1(A[28]), .out(multiplexer_3_out), .sel(Move[0]));
  Multiplexer #(.enable("false")) multiplexer_4 (.in0(A[28]), .in1(A[27]), .out(multiplexer_4_out), .sel(Move[0]));
  Multiplexer #(.enable("false")) multiplexer_5 (.in0(A[27]), .in1(A[26]), .out(multiplexer_5_out), .sel(Move[0]));
  Multiplexer #(.enable("false")) multiplexer_6 (.in0(A[26]), .in1(A[25]), .out(multiplexer_6_out), .sel(Move[0]));
  Multiplexer #(.enable("false")) multiplexer_7 (.in0(A[25]), .in1(A[24]), .out(multiplexer_7_out), .sel(Move[0]));
  Multiplexer #(.enable("false")) multiplexer_8 (.in0(A[24]), .in1(A[23]), .out(multiplexer_8_out), .sel(Move[0]));
  Multiplexer #(.enable("false")) multiplexer_9 (.in0(A[23]), .in1(A[22]), .out(multiplexer_9_out), .sel(Move[0]));
  Multiplexer #(.enable("false")) multiplexer_10 (.in0(A[22]), .in1(A[21]), .out(multiplexer_10_out), .sel(Move[0]));
  Multiplexer #(.enable("false")) multiplexer_11 (.in0(A[21]), .in1(A[20]), .out(multiplexer_11_out), .sel(Move[0]));
  Multiplexer #(.enable("false")) multiplexer_12 (.in0(A[20]), .in1(A[19]), .out(multiplexer_12_out), .sel(Move[0]));
  Multiplexer #(.enable("false")) multiplexer_13 (.in0(A[19]), .in1(A[18]), .out(multiplexer_13_out), .sel(Move[0]));
  Multiplexer #(.enable("false")) multiplexer_14 (.in0(A[18]), .in1(A[17]), .out(multiplexer_14_out), .sel(Move[0]));
  Multiplexer #(.enable("false")) multiplexer_15 (.in0(A[17]), .in1(A[16]), .out(multiplexer_15_out), .sel(Move[0]));
  Multiplexer #(.enable("false")) multiplexer_16 (.in0(A[16]), .in1(A[15]), .out(multiplexer_16_out), .sel(Move[0]));
  Multiplexer #(.enable("false")) multiplexer_17 (.in0(A[15]), .in1(A[14]), .out(multiplexer_17_out), .sel(Move[0]));
  Multiplexer #(.enable("false")) multiplexer_18 (.in0(A[14]), .in1(A[13]), .out(multiplexer_18_out), .sel(Move[0]));
  Multiplexer #(.enable("false")) multiplexer_19 (.in0(A[13]), .in1(A[12]), .out(multiplexer_19_out), .sel(Move[0]));
  Multiplexer #(.enable("false")) multiplexer_20 (.in0(A[12]), .in1(A[11]), .out(multiplexer_20_out), .sel(Move[0]));
  Multiplexer #(.enable("false")) multiplexer_21 (.in0(A[11]), .in1(A[10]), .out(multiplexer_21_out), .sel(Move[0]));
  Multiplexer #(.enable("false")) multiplexer_22 (.in0(A[10]), .in1(A[9]), .out(multiplexer_22_out), .sel(Move[0]));
  Multiplexer #(.enable("false")) multiplexer_23 (.in0(A[9]), .in1(A[8]), .out(multiplexer_23_out), .sel(Move[0]));
  Multiplexer #(.enable("false")) multiplexer_24 (.in0(A[8]), .in1(A[7]), .out(multiplexer_24_out), .sel(Move[0]));
  Multiplexer #(.enable("false")) multiplexer_25 (.in0(A[7]), .in1(A[6]), .out(multiplexer_25_out), .sel(Move[0]));
  Multiplexer #(.enable("false")) multiplexer_26 (.in0(A[6]), .in1(A[5]), .out(multiplexer_26_out), .sel(Move[0]));
  Multiplexer #(.enable("false")) multiplexer_27 (.in0(A[5]), .in1(A[4]), .out(multiplexer_27_out), .sel(Move[0]));
  Multiplexer #(.enable("false")) multiplexer_28 (.in0(A[4]), .in1(A[3]), .out(multiplexer_28_out), .sel(Move[0]));
  Multiplexer #(.enable("false")) multiplexer_29 (.in0(A[3]), .in1(A[2]), .out(multiplexer_29_out), .sel(Move[0]));
  Multiplexer #(.enable("false")) multiplexer_30 (.in0(A[2]), .in1(A[1]), .out(multiplexer_30_out), .sel(Move[0]));
  Multiplexer #(.enable("false")) multiplexer_31 (.in0(A[1]), .in1(A[0]), .out(multiplexer_31_out), .sel(Move[0]));
  Multiplexer #(.enable("false")) multiplexer_32 (.in0(A[0]), .in1(A[31]), .out(multiplexer_32_out), .sel(Move[0]));
  Multiplexer #(.enable("false")) multiplexer_33 (
    .in0(multiplexer_1_out), .in1(multiplexer_3_out), .out(multiplexer_33_out), .sel(Move[1]));
  Multiplexer #(.enable("false")) multiplexer_34 (
    .in0(multiplexer_2_out), .in1(multiplexer_4_out), .out(multiplexer_34_out), .sel(Move[1]));
  Multiplexer #(.enable("false")) multiplexer_35 (
    .in0(multiplexer_3_out), .in1(multiplexer_5_out), .out(multiplexer_35_out), .sel(Move[1]));
  Multiplexer #(.enable("false")) multiplexer_36 (
    .in0(multiplexer_4_out), .in1(multiplexer_6_out), .out(multiplexer_36_out), .sel(Move[1]));
  Multiplexer #(.enable("false")) multiplexer_37 (
    .in0(multiplexer_5_out), .in1(multiplexer_7_out), .out(multiplexer_37_out), .sel(Move[1]));
  Multiplexer #(.enable("false")) multiplexer_38 (
    .in0(multiplexer_6_out), .in1(multiplexer_8_out), .out(multiplexer_38_out), .sel(Move[1]));
  Multiplexer #(.enable("false")) multiplexer_39 (
    .in0(multiplexer_7_out), .in1(multiplexer_9_out), .out(multiplexer_39_out), .sel(Move[1]));
  Multiplexer #(.enable("false")) multiplexer_40 (
    .in0(multiplexer_8_out), .in1(multiplexer_10_out), .out(multiplexer_40_out), .sel(Move[1]));
  Multiplexer #(.enable("false")) multiplexer_41 (
    .in0(multiplexer_9_out), .in1(multiplexer_11_out), .out(multiplexer_41_out), .sel(Move[1]));
  Multiplexer #(.enable("false")) multiplexer_42 (
    .in0(multiplexer_10_out), .in1(multiplexer_12_out), .out(multiplexer_42_out), .sel(Move[1]));
  Multiplexer #(.enable("false")) multiplexer_43 (
    .in0(multiplexer_11_out), .in1(multiplexer_13_out), .out(multiplexer_43_out), .sel(Move[1]));
  Multiplexer #(.enable("false")) multiplexer_44 (
    .in0(multiplexer_12_out), .in1(multiplexer_14_out), .out(multiplexer_44_out), .sel(Move[1]));
  Multiplexer #(.enable("false")) multiplexer_45 (
    .in0(multiplexer_13_out), .in1(multiplexer_15_out), .out(multiplexer_45_out), .sel(Move[1]));
  Multiplexer #(.enable("false")) multiplexer_46 (
    .in0(multiplexer_14_out), .in1(multiplexer_16_out), .out(multiplexer_46_out), .sel(Move[1]));
  Multiplexer #(.enable("false")) multiplexer_47 (
    .in0(multiplexer_15_out), .in1(multiplexer_17_out), .out(multiplexer_47_out), .sel(Move[1]));
  Multiplexer #(.enable("false")) multiplexer_48 (
    .in0(multiplexer_16_out), .in1(multiplexer_18_out), .out(multiplexer_48_out), .sel(Move[1]));
  Multiplexer #(.enable("false")) multiplexer_49 (
    .in0(multiplexer_17_out), .in1(multiplexer_19_out), .out(multiplexer_49_out), .sel(Move[1]));
  Multiplexer #(.enable("false")) multiplexer_50 (
    .in0(multiplexer_18_out), .in1(multiplexer_20_out), .out(multiplexer_50_out), .sel(Move[1]));
  Multiplexer #(.enable("false")) multiplexer_51 (
    .in0(multiplexer_19_out), .in1(multiplexer_21_out), .out(multiplexer_51_out), .sel(Move[1]));
  Multiplexer #(.enable("false")) multiplexer_52 (
    .in0(multiplexer_20_out), .in1(multiplexer_22_out), .out(multiplexer_52_out), .sel(Move[1]));
  Multiplexer #(.enable("false")) multiplexer_53 (
    .in0(multiplexer_21_out), .in1(multiplexer_23_out), .out(multiplexer_53_out), .sel(Move[1]));
  Multiplexer #(.enable("false")) multiplexer_54 (
    .in0(multiplexer_22_out), .in1(multiplexer_24_out), .out(multiplexer_54_out), .sel(Move[1]));
  Multiplexer #(.enable("false")) multiplexer_55 (
    .in0(multiplexer_23_out), .in1(multiplexer_25_out), .out(multiplexer_55_out), .sel(Move[1]));
  Multiplexer #(.enable("false")) multiplexer_56 (
    .in0(multiplexer_24_out), .in1(multiplexer_26_out), .out(multiplexer_56_out), .sel(Move[1]));
  Multiplexer #(.enable("false")) multiplexer_57 (
    .in0(multiplexer_25_out), .in1(multiplexer_27_out), .out(multiplexer_57_out), .sel(Move[1]));
  Multiplexer #(.enable("false")) multiplexer_58 (
    .in0(multiplexer_26_out), .in1(multiplexer_28_out), .out(multiplexer_58_out), .sel(Move[1]));
  Multiplexer #(.enable("false")) multiplexer_59 (
    .in0(multiplexer_27_out), .in1(multiplexer_29_out), .out(multiplexer_59_out), .sel(Move[1]));
  Multiplexer #(.enable("false")) multiplexer_60 (
    .in0(multiplexer_28_out), .in1(multiplexer_30_out), .out(multiplexer_60_out), .sel(Move[1]));
  Multiplexer #(.enable("false")) multiplexer_61 (
    .in0(multiplexer_29_out), .in1(multiplexer_31_out), .out(multiplexer_61_out), .sel(Move[1]));
  Multiplexer #(.enable("false")) multiplexer_62 (
    .in0(multiplexer_30_out), .in1(multiplexer_32_out), .out(multiplexer_62_out), .sel(Move[1]));
  Multiplexer #(.enable("false")) multiplexer_63 (
    .in0(multiplexer_31_out), .in1(multiplexer_1_out), .out(multiplexer_63_out), .sel(Move[1]));
  Multiplexer #(.enable("false")) multiplexer_64 (
    .in0(multiplexer_32_out), .in1(multiplexer_2_out), .out(multiplexer_64_out), .sel(Move[1]));
  Multiplexer #(.enable("false")) multiplexer_65 (
    .in0(multiplexer_33_out), .in1(multiplexer_37_out), .out(multiplexer_65_out), .sel(Move[2]));
  Multiplexer #(.enable("false")) multiplexer_66 (
    .in0(multiplexer_34_out), .in1(multiplexer_38_out), .out(multiplexer_66_out), .sel(Move[2]));
  Multiplexer #(.enable("false")) multiplexer_67 (
    .in0(multiplexer_35_out), .in1(multiplexer_39_out), .out(multiplexer_67_out), .sel(Move[2]));
  Multiplexer #(.enable("false")) multiplexer_68 (
    .in0(multiplexer_36_out), .in1(multiplexer_40_out), .out(multiplexer_68_out), .sel(Move[2]));
  Multiplexer #(.enable("false")) multiplexer_69 (
    .in0(multiplexer_37_out), .in1(multiplexer_41_out), .out(multiplexer_69_out), .sel(Move[2]));
  Multiplexer #(.enable("false")) multiplexer_70 (
    .in0(multiplexer_38_out), .in1(multiplexer_42_out), .out(multiplexer_70_out), .sel(Move[2]));
  Multiplexer #(.enable("false")) multiplexer_71 (
    .in0(multiplexer_39_out), .in1(multiplexer_43_out), .out(multiplexer_71_out), .sel(Move[2]));
  Multiplexer #(.enable("false")) multiplexer_72 (
    .in0(multiplexer_40_out), .in1(multiplexer_44_out), .out(multiplexer_72_out), .sel(Move[2]));
  Multiplexer #(.enable("false")) multiplexer_73 (
    .in0(multiplexer_41_out), .in1(multiplexer_45_out), .out(multiplexer_73_out), .sel(Move[2]));
  Multiplexer #(.enable("false")) multiplexer_74 (
    .in0(multiplexer_42_out), .in1(multiplexer_46_out), .out(multiplexer_74_out), .sel(Move[2]));
  Multiplexer #(.enable("false")) multiplexer_75 (
    .in0(multiplexer_43_out), .in1(multiplexer_47_out), .out(multiplexer_75_out), .sel(Move[2]));
  Multiplexer #(.enable("false")) multiplexer_76 (
    .in0(multiplexer_44_out), .in1(multiplexer_48_out), .out(multiplexer_76_out), .sel(Move[2]));
  Multiplexer #(.enable("false")) multiplexer_77 (
    .in0(multiplexer_45_out), .in1(multiplexer_49_out), .out(multiplexer_77_out), .sel(Move[2]));
  Multiplexer #(.enable("false")) multiplexer_78 (
    .in0(multiplexer_46_out), .in1(multiplexer_50_out), .out(multiplexer_78_out), .sel(Move[2]));
  Multiplexer #(.enable("false")) multiplexer_79 (
    .in0(multiplexer_47_out), .in1(multiplexer_51_out), .out(multiplexer_79_out), .sel(Move[2]));
  Multiplexer #(.enable("false")) multiplexer_80 (
    .in0(multiplexer_48_out), .in1(multiplexer_52_out), .out(multiplexer_80_out), .sel(Move[2]));
  Multiplexer #(.enable("false")) multiplexer_81 (
    .in0(multiplexer_49_out), .in1(multiplexer_53_out), .out(multiplexer_81_out), .sel(Move[2]));
  Multiplexer #(.enable("false")) multiplexer_82 (
    .in0(multiplexer_50_out), .in1(multiplexer_54_out), .out(multiplexer_82_out), .sel(Move[2]));
  Multiplexer #(.enable("false")) multiplexer_83 (
    .in0(multiplexer_51_out), .in1(multiplexer_55_out), .out(multiplexer_83_out), .sel(Move[2]));
  Multiplexer #(.enable("false")) multiplexer_84 (
    .in0(multiplexer_52_out), .in1(multiplexer_56_out), .out(multiplexer_84_out), .sel(Move[2]));
  Multiplexer #(.enable("false")) multiplexer_85 (
    .in0(multiplexer_53_out), .in1(multiplexer_57_out), .out(multiplexer_85_out), .sel(Move[2]));
  Multiplexer #(.enable("false")) multiplexer_86 (
    .in0(multiplexer_54_out), .in1(multiplexer_58_out), .out(multiplexer_86_out), .sel(Move[2]));
  Multiplexer #(.enable("false")) multiplexer_87 (
    .in0(multiplexer_55_out), .in1(multiplexer_59_out), .out(multiplexer_87_out), .sel(Move[2]));
  Multiplexer #(.enable("false")) multiplexer_88 (
    .in0(multiplexer_56_out), .in1(multiplexer_60_out), .out(multiplexer_88_out), .sel(Move[2]));
  Multiplexer #(.enable("false")) multiplexer_89 (
    .in0(multiplexer_57_out), .in1(multiplexer_61_out), .out(multiplexer_89_out), .sel(Move[2]));
  Multiplexer #(.enable("false")) multiplexer_90 (
    .in0(multiplexer_58_out), .in1(multiplexer_62_out), .out(multiplexer_90_out), .sel(Move[2]));
  Multiplexer #(.enable("false")) multiplexer_91 (
    .in0(multiplexer_59_out), .in1(multiplexer_63_out), .out(multiplexer_91_out), .sel(Move[2]));
  Multiplexer #(.enable("false")) multiplexer_92 (
    .in0(multiplexer_60_out), .in1(multiplexer_64_out), .out(multiplexer_92_out), .sel(Move[2]));
  Multiplexer #(.enable("false")) multiplexer_93 (
    .in0(multiplexer_61_out), .in1(multiplexer_33_out), .out(multiplexer_93_out), .sel(Move[2]));
  Multiplexer #(.enable("false")) multiplexer_94 (
    .in0(multiplexer_62_out), .in1(multiplexer_34_out), .out(multiplexer_94_out), .sel(Move[2]));
  Multiplexer #(.enable("false")) multiplexer_95 (
    .in0(multiplexer_63_out), .in1(multiplexer_35_out), .out(multiplexer_95_out), .sel(Move[2]));
  Multiplexer #(.enable("false")) multiplexer_96 (
    .in0(multiplexer_64_out), .in1(multiplexer_36_out), .out(multiplexer_96_out), .sel(Move[2]));
  Multiplexer #(.enable("false")) multiplexer_97 (
    .in0(multiplexer_65_out), .in1(multiplexer_73_out), .out(multiplexer_97_out), .sel(Move[3]));
  Multiplexer #(.enable("false")) multiplexer_98 (
    .in0(multiplexer_66_out), .in1(multiplexer_74_out), .out(multiplexer_98_out), .sel(Move[3]));
  Multiplexer #(.enable("false")) multiplexer_99 (
    .in0(multiplexer_67_out), .in1(multiplexer_75_out), .out(multiplexer_99_out), .sel(Move[3]));
  Multiplexer #(.enable("false")) multiplexer_100 (
    .in0(multiplexer_68_out), .in1(multiplexer_76_out), .out(multiplexer_100_out), .sel(Move[3]));
  Multiplexer #(.enable("false")) multiplexer_101 (
    .in0(multiplexer_69_out), .in1(multiplexer_77_out), .out(multiplexer_101_out), .sel(Move[3]));
  Multiplexer #(.enable("false")) multiplexer_102 (
    .in0(multiplexer_70_out), .in1(multiplexer_78_out), .out(multiplexer_102_out), .sel(Move[3]));
  Multiplexer #(.enable("false")) multiplexer_103 (
    .in0(multiplexer_71_out), .in1(multiplexer_79_out), .out(multiplexer_103_out), .sel(Move[3]));
  Multiplexer #(.enable("false")) multiplexer_104 (
    .in0(multiplexer_72_out), .in1(multiplexer_80_out), .out(multiplexer_104_out), .sel(Move[3]));
  Multiplexer #(.enable("false")) multiplexer_105 (
    .in0(multiplexer_73_out), .in1(multiplexer_81_out), .out(multiplexer_105_out), .sel(Move[3]));
  Multiplexer #(.enable("false")) multiplexer_106 (
    .in0(multiplexer_74_out), .in1(multiplexer_82_out), .out(multiplexer_106_out), .sel(Move[3]));
  Multiplexer #(.enable("false")) multiplexer_107 (
    .in0(multiplexer_75_out), .in1(multiplexer_83_out), .out(multiplexer_107_out), .sel(Move[3]));
  Multiplexer #(.enable("false")) multiplexer_108 (
    .in0(multiplexer_76_out), .in1(multiplexer_84_out), .out(multiplexer_108_out), .sel(Move[3]));
  Multiplexer #(.enable("false")) multiplexer_109 (
    .in0(multiplexer_77_out), .in1(multiplexer_85_out), .out(multiplexer_109_out), .sel(Move[3]));
  Multiplexer #(.enable("false")) multiplexer_110 (
    .in0(multiplexer_78_out), .in1(multiplexer_86_out), .out(multiplexer_110_out), .sel(Move[3]));
  Multiplexer #(.enable("false")) multiplexer_111 (
    .in0(multiplexer_79_out), .in1(multiplexer_87_out), .out(multiplexer_111_out), .sel(Move[3]));
  Multiplexer #(.enable("false")) multiplexer_112 (
    .in0(multiplexer_80_out), .in1(multiplexer_88_out), .out(multiplexer_112_out), .sel(Move[3]));
  Multiplexer #(.enable("false")) multiplexer_113 (
    .in0(multiplexer_81_out), .in1(multiplexer_89_out), .out(multiplexer_113_out), .sel(Move[3]));
  Multiplexer #(.enable("false")) multiplexer_114 (
    .in0(multiplexer_82_out), .in1(multiplexer_90_out), .out(multiplexer_114_out), .sel(Move[3]));
  Multiplexer #(.enable("false")) multiplexer_115 (
    .in0(multiplexer_83_out), .in1(multiplexer_91_out), .out(multiplexer_115_out), .sel(Move[3]));
  Multiplexer #(.enable("false")) multiplexer_116 (
    .in0(multiplexer_84_out), .in1(multiplexer_92_out), .out(multiplexer_116_out), .sel(Move[3]));
  Multiplexer #(.enable("false")) multiplexer_117 (
    .in0(multiplexer_85_out), .in1(multiplexer_93_out), .out(multiplexer_117_out), .sel(Move[3]));
  Multiplexer #(.enable("false")) multiplexer_118 (
    .in0(multiplexer_86_out), .in1(multiplexer_94_out), .out(multiplexer_118_out), .sel(Move[3]));
  Multiplexer #(.enable("false")) multiplexer_119 (
    .in0(multiplexer_87_out), .in1(multiplexer_95_out), .out(multiplexer_119_out), .sel(Move[3]));
  Multiplexer #(.enable("false")) multiplexer_120 (
    .in0(multiplexer_88_out), .in1(multiplexer_96_out), .out(multiplexer_120_out), .sel(Move[3]));
  Multiplexer #(.enable("false")) multiplexer_121 (
    .in0(multiplexer_89_out), .in1(multiplexer_65_out), .out(multiplexer_121_out), .sel(Move[3]));
  Multiplexer #(.enable("false")) multiplexer_122 (
    .in0(multiplexer_90_out), .in1(multiplexer_66_out), .out(multiplexer_122_out), .sel(Move[3]));
  Multiplexer #(.enable("false")) multiplexer_123 (
    .in0(multiplexer_91_out), .in1(multiplexer_67_out), .out(multiplexer_123_out), .sel(Move[3]));
  Multiplexer #(.enable("false")) multiplexer_124 (
    .in0(multiplexer_92_out), .in1(multiplexer_68_out), .out(multiplexer_124_out), .sel(Move[3]));
  Multiplexer #(.enable("false")) multiplexer_125 (
    .in0(multiplexer_93_out), .in1(multiplexer_69_out), .out(multiplexer_125_out), .sel(Move[3]));
  Multiplexer #(.enable("false")) multiplexer_126 (
    .in0(multiplexer_94_out), .in1(multiplexer_70_out), .out(multiplexer_126_out), .sel(Move[3]));
  Multiplexer #(.enable("false")) multiplexer_127 (
    .in0(multiplexer_95_out), .in1(multiplexer_71_out), .out(multiplexer_127_out), .sel(Move[3]));
  Multiplexer #(.enable("false")) multiplexer_128 (
    .in0(multiplexer_96_out), .in1(multiplexer_72_out), .out(multiplexer_128_out), .sel(Move[3]));
  Multiplexer #(.enable("false")) multiplexer_129 (
    .in0(multiplexer_97_out), .in1(multiplexer_113_out), .out(S[31]), .sel(Move[4]));
  Multiplexer #(.enable("false")) multiplexer_130 (
    .in0(multiplexer_98_out), .in1(multiplexer_114_out), .out(S[30]), .sel(Move[4]));
  Multiplexer #(.enable("false")) multiplexer_131 (
    .in0(multiplexer_99_out), .in1(multiplexer_115_out), .out(S[29]), .sel(Move[4]));
  Multiplexer #(.enable("false")) multiplexer_132 (
    .in0(multiplexer_100_out), .in1(multiplexer_116_out), .out(S[28]), .sel(Move[4]));
  Multiplexer #(.enable("false")) multiplexer_133 (
    .in0(multiplexer_101_out), .in1(multiplexer_117_out), .out(S[27]), .sel(Move[4]));
  Multiplexer #(.enable("false")) multiplexer_134 (
    .in0(multiplexer_102_out), .in1(multiplexer_118_out), .out(S[26]), .sel(Move[4]));
  Multiplexer #(.enable("false")) multiplexer_135 (
    .in0(multiplexer_103_out), .in1(multiplexer_119_out), .out(S[25]), .sel(Move[4]));
  Multiplexer #(.enable("false")) multiplexer_136 (
    .in0(multiplexer_104_out), .in1(multiplexer_120_out), .out(S[24]), .sel(Move[4]));
  Multiplexer #(.enable("false")) multiplexer_137 (
    .in0(multiplexer_105_out), .in1(multiplexer_121_out), .out(S[23]), .sel(Move[4]));
  Multiplexer #(.enable("false")) multiplexer_138 (
    .in0(multiplexer_106_out), .in1(multiplexer_122_out), .out(S[22]), .sel(Move[4]));
  Multiplexer #(.enable("false")) multiplexer_139 (
    .in0(multiplexer_107_out), .in1(multiplexer_123_out), .out(S[21]), .sel(Move[4]));
  Multiplexer #(.enable("false")) multiplexer_140 (
    .in0(multiplexer_108_out), .in1(multiplexer_124_out), .out(S[20]), .sel(Move[4]));
  Multiplexer #(.enable("false")) multiplexer_141 (
    .in0(multiplexer_109_out), .in1(multiplexer_125_out), .out(S[19]), .sel(Move[4]));
  Multiplexer #(.enable("false")) multiplexer_142 (
    .in0(multiplexer_110_out), .in1(multiplexer_126_out), .out(S[18]), .sel(Move[4]));
  Multiplexer #(.enable("false")) multiplexer_143 (
    .in0(multiplexer_111_out), .in1(multiplexer_127_out), .out(S[17]), .sel(Move[4]));
  Multiplexer #(.enable("false")) multiplexer_144 (
    .in0(multiplexer_112_out), .in1(multiplexer_128_out), .out(S[16]), .sel(Move[4]));
  Multiplexer #(.enable("false")) multiplexer_145 (
    .in0(multiplexer_113_out), .in1(multiplexer_97_out), .out(S[15]), .sel(Move[4]));
  Multiplexer #(.enable("false")) multiplexer_146 (
    .in0(multiplexer_114_out), .in1(multiplexer_98_out), .out(S[14]), .sel(Move[4]));
  Multiplexer #(.enable("false")) multiplexer_147 (
    .in0(multiplexer_115_out), .in1(multiplexer_99_out), .out(S[13]), .sel(Move[4]));
  Multiplexer #(.enable("false")) multiplexer_148 (
    .in0(multiplexer_116_out), .in1(multiplexer_100_out), .out(S[12]), .sel(Move[4]));
  Multiplexer #(.enable("false")) multiplexer_149 (
    .in0(multiplexer_117_out), .in1(multiplexer_101_out), .out(S[11]), .sel(Move[4]));
  Multiplexer #(.enable("false")) multiplexer_150 (
    .in0(multiplexer_118_out), .in1(multiplexer_102_out), .out(S[10]), .sel(Move[4]));
  Multiplexer #(.enable("false")) multiplexer_151 (
    .in0(multiplexer_119_out), .in1(multiplexer_103_out), .out(S[9]), .sel(Move[4]));
  Multiplexer #(.enable("false")) multiplexer_152 (
    .in0(multiplexer_120_out), .in1(multiplexer_104_out), .out(S[8]), .sel(Move[4]));
  Multiplexer #(.enable("false")) multiplexer_153 (
    .in0(multiplexer_121_out), .in1(multiplexer_105_out), .out(S[7]), .sel(Move[4]));
  Multiplexer #(.enable("false")) multiplexer_154 (
    .in0(multiplexer_122_out), .in1(multiplexer_106_out), .out(S[6]), .sel(Move[4]));
  Multiplexer #(.enable("false")) multiplexer_155 (
    .in0(multiplexer_123_out), .in1(multiplexer_107_out), .out(S[5]), .sel(Move[4]));
  Multiplexer #(.enable("false")) multiplexer_156 (
    .in0(multiplexer_124_out), .in1(multiplexer_108_out), .out(S[4]), .sel(Move[4]));
  Multiplexer #(.enable("false")) multiplexer_157 (
    .in0(multiplexer_125_out), .in1(multiplexer_109_out), .out(S[3]), .sel(Move[4]));
  Multiplexer #(.enable("false")) multiplexer_158 (
    .in0(multiplexer_126_out), .in1(multiplexer_110_out), .out(S[2]), .sel(Move[4]));
  Multiplexer #(.enable("false")) multiplexer_159 (
    .in0(multiplexer_127_out), .in1(multiplexer_111_out), .out(S[1]), .sel(Move[4]));
  Multiplexer #(.enable("false")) multiplexer_160 (
    .in0(multiplexer_128_out), .in1(multiplexer_112_out), .out(S[0]), .sel(Move[4]));
endmodule

module pc (
  input  Clk,
  input  RESET,
  input  Jump,
  input  [7:0] Const,
  output [7:0] Addr
);

  wire [7:0] adder_1_out, multiplexer_1_out;

  Multiplexer #(.width(8), .enable("false")) multiplexer_1 (
    .in0(8'h1), .in1(Const), .out(multiplexer_1_out), .sel(Jump));
  Adder adder_1 (.a(Addr), .b(multiplexer_1_out), .out(adder_1_out), .cin(1'b0));  // open: cout
  Register register_1 (.D(adder_1_out), .Q(Addr), .clk(Clk), .clr(RESET));  // open: en
endmodule

module SLT (
  input  [4:0] OpeCode,
  input  [31:0] Sin,
  output [31:0] Sout
);

  wire and_1_out;

  and and_1 (and_1_out, OpeCode[0], OpeCode[1], ~OpeCode[2], OpeCode[3], ~OpeCode[4]);  // AND_Gate
  Multiplexer #(.width(32), .enable("false")) multiplexer_1 (
    .in0(Sin), .in1({{31{1'b0}}, Sin[31]}), .out(Sout), .sel(and_1_out));
endmodule
